// Logisim project LambdaCalculus.circ as structural Verilog: 19 circuits, main circuit main
module main (
  input  CLK
);


  // Notes on the sheet:
  //   4,4
  //   Resolve Flag: [Flag State]
  //   [1-bit]
  //   Expression Data: [Resolve Flag, Expression Type, Child Left, Child right]
  //   1,3,4,4
  //   Instruction Data: [Instruction, Address Contents]
  //   [8-bit]
  //   Reduce Flag: [Flag State]
  //   [1-bit]
  //   [12-bit]
  //   22-bit bus
  //   Expression Type
  //   Undefined: 000
  //   Name: 001
  //   Application: 010
  //   Function: 011
  //   Goto: 100
  //   [Expression, Instruction, Resolve, Reduce]
endmodule

module Selector (
  input  [21:0] SelfBusInput,
  input  NewNodeReturn,
  input  [3:0] NewNodeReturn_2,
  input  [21:0] IN1,
  input  CLK,
  input  [21:0] IN1_2,
  input  [3:0] UniqueNodeID,
  input  [21:0] IN2,
  input  [21:0] IN2_2,
  input  [21:0] IN3,
  input  [21:0] IN3_2,
  input  [21:0] IN4,
  input  [21:0] IN4_2,
  input  [21:0] IN5,
  input  [21:0] IN5_2,
  input  [21:0] IN6,
  input  [21:0] IN6_2,
  input  [21:0] IN7,
  input  [21:0] IN7_2,
  input  [21:0] IN8,
  input  [21:0] IN8_2,
  input  [21:0] IN9,
  input  [21:0] IN9_2,
  input  [21:0] IN10,
  input  [21:0] IN10_2,
  input  [21:0] IN11,
  input  [21:0] IN11_2,
  input  [21:0] IN12,
  input  [21:0] IN12_2,
  input  [21:0] IN13,
  input  [21:0] IN13_2,
  input  [21:0] IN14,
  input  [21:0] IN14_2,
  input  [21:0] IN15,
  input  [21:0] IN15_2,
  output NewNodeRequest,
  output [21:0] SelfBusOutput,
  output [2:0] CurrentExpressionType,
  output CurrentResolveState,
  output [21:0] OUT1,
  output [21:0] OUT1_2,
  output [21:0] OUT2,
  output [21:0] OUT2_2,
  output [21:0] OUT3,
  output [21:0] OUT3_2,
  output [21:0] OUT4,
  output [21:0] OUT4_2,
  output [21:0] OUT5,
  output [21:0] OUT5_2,
  output [21:0] OUT6,
  output [21:0] OUT6_2,
  output [21:0] OUT7,
  output [21:0] OUT7_2,
  output [21:0] OUT8,
  output [21:0] OUT8_2,
  output [21:0] OUT9,
  output [21:0] OUT9_2,
  output [21:0] OUT10,
  output [21:0] OUT10_2,
  output [21:0] OUT11,
  output [21:0] OUT11_2,
  output [21:0] OUT12,
  output [21:0] OUT12_2,
  output [21:0] OUT13,
  output [21:0] OUT13_2,
  output [21:0] OUT14,
  output [21:0] OUT14_2,
  output [21:0] OUT15,
  output [21:0] OUT15_2
);

  wire decoder_1_out0, decoder_1_out1, decoder_1_out2, decoder_1_out3, decoder_1_out4, decoder_1_out5,
       decoder_1_out6, decoder_1_out7, decoder_1_out8, decoder_1_out9, decoder_1_out10, decoder_1_out11,
       decoder_1_out12, decoder_1_out13, decoder_1_out14, decoder_1_out15, decoder_2_out0, decoder_2_out1,
       decoder_2_out2, decoder_2_out3, decoder_2_out4, decoder_2_out5, decoder_2_out6, decoder_2_out7,
       decoder_2_out8, decoder_2_out9, decoder_2_out10, decoder_2_out11, decoder_2_out12, decoder_2_out13,
       decoder_2_out14, decoder_2_out15;
  wire [3:0] node_1_childleftpointerout, node_1_childrightpointerout;
  wire [21:0] controlled_buffer_1_out, controlled_buffer_31_out, node_1_childleftout, node_1_childrightout;

  assign controlled_buffer_1_out = decoder_1_out1 ? IN1 : 22'bz;  // Controlled_Buffer controlled_buffer_1
  assign OUT1 = decoder_1_out1 ? node_1_childleftout : 22'bz;  // Controlled_Buffer controlled_buffer_2
  assign controlled_buffer_1_out = decoder_1_out2 ? IN2 : 22'bz;  // Controlled_Buffer controlled_buffer_3
  assign OUT2 = decoder_1_out2 ? node_1_childleftout : 22'bz;  // Controlled_Buffer controlled_buffer_4
  assign controlled_buffer_1_out = decoder_1_out3 ? IN3 : 22'bz;  // Controlled_Buffer controlled_buffer_5
  assign OUT3 = decoder_1_out3 ? node_1_childleftout : 22'bz;  // Controlled_Buffer controlled_buffer_6
  assign controlled_buffer_1_out = decoder_1_out4 ? IN4 : 22'bz;  // Controlled_Buffer controlled_buffer_7
  assign OUT4 = decoder_1_out4 ? node_1_childleftout : 22'bz;  // Controlled_Buffer controlled_buffer_8
  Decoder #(.select(4)) decoder_1 (
    .out0(decoder_1_out0), .out1(decoder_1_out1), .out2(decoder_1_out2), .out3(decoder_1_out3),
    .out4(decoder_1_out4), .out5(decoder_1_out5), .out6(decoder_1_out6), .out7(decoder_1_out7),
    .out8(decoder_1_out8), .out9(decoder_1_out9), .out10(decoder_1_out10), .out11(decoder_1_out11),
    .out12(decoder_1_out12), .out13(decoder_1_out13), .out14(decoder_1_out14), .out15(decoder_1_out15),
    .sel(node_1_childleftpointerout));  // open: en
  assign controlled_buffer_1_out = decoder_1_out5 ? IN5 : 22'bz;  // Controlled_Buffer controlled_buffer_9
  assign OUT5 = decoder_1_out5 ? node_1_childleftout : 22'bz;  // Controlled_Buffer controlled_buffer_10
  assign controlled_buffer_1_out = decoder_1_out6 ? IN6 : 22'bz;  // Controlled_Buffer controlled_buffer_11
  assign OUT6 = decoder_1_out6 ? node_1_childleftout : 22'bz;  // Controlled_Buffer controlled_buffer_12
  assign controlled_buffer_1_out = decoder_1_out7 ? IN7 : 22'bz;  // Controlled_Buffer controlled_buffer_13
  assign OUT7 = decoder_1_out7 ? node_1_childleftout : 22'bz;  // Controlled_Buffer controlled_buffer_14
  assign controlled_buffer_1_out = decoder_1_out8 ? IN8 : 22'bz;  // Controlled_Buffer controlled_buffer_15
  assign OUT8 = decoder_1_out8 ? node_1_childleftout : 22'bz;  // Controlled_Buffer controlled_buffer_16
  assign controlled_buffer_1_out = decoder_1_out9 ? IN9 : 22'bz;  // Controlled_Buffer controlled_buffer_17
  assign OUT9 = decoder_1_out9 ? node_1_childleftout : 22'bz;  // Controlled_Buffer controlled_buffer_18
  assign controlled_buffer_1_out = decoder_1_out10 ? IN10 : 22'bz;  // Controlled_Buffer controlled_buffer_19
  assign OUT10 = decoder_1_out10 ? node_1_childleftout : 22'bz;  // Controlled_Buffer controlled_buffer_20
  assign controlled_buffer_1_out = decoder_1_out11 ? IN11 : 22'bz;  // Controlled_Buffer controlled_buffer_21
  assign OUT11 = decoder_1_out11 ? node_1_childleftout : 22'bz;  // Controlled_Buffer controlled_buffer_22
  assign controlled_buffer_1_out = decoder_1_out12 ? IN12 : 22'bz;  // Controlled_Buffer controlled_buffer_23
  assign OUT12 = decoder_1_out12 ? node_1_childleftout : 22'bz;  // Controlled_Buffer controlled_buffer_24
  assign controlled_buffer_1_out = decoder_1_out13 ? IN13 : 22'bz;  // Controlled_Buffer controlled_buffer_25
  assign OUT13 = decoder_1_out13 ? node_1_childleftout : 22'bz;  // Controlled_Buffer controlled_buffer_26
  assign controlled_buffer_1_out = decoder_1_out14 ? IN14 : 22'bz;  // Controlled_Buffer controlled_buffer_27
  assign OUT14 = decoder_1_out14 ? node_1_childleftout : 22'bz;  // Controlled_Buffer controlled_buffer_28
  assign controlled_buffer_1_out = decoder_1_out15 ? IN15 : 22'bz;  // Controlled_Buffer controlled_buffer_29
  assign OUT15 = decoder_1_out15 ? node_1_childleftout : 22'bz;  // Controlled_Buffer controlled_buffer_30
  Node node_1 (
    .ChildLeftIn(controlled_buffer_1_out), .ChildLeftOut(node_1_childleftout),
    .ChildLeftPointerOut(node_1_childleftpointerout), .ParentIn(SelfBusInput),
    .CurrentResolveState(CurrentResolveState), .CurrentExpressionType(CurrentExpressionType),
    .NewNodeRequest(NewNodeRequest), .NewNodeReturn(NewNodeReturn), .NewID(NewNodeReturn_2),
    .ParentOut(SelfBusOutput), .Clock(CLK), .UniqueNodeID(UniqueNodeID),
    .ChildRightIn(controlled_buffer_31_out), .ChildRightOut(node_1_childrightout),
    .ChildRightPointerOut(node_1_childrightpointerout));
  assign controlled_buffer_31_out = decoder_2_out1 ? IN14_2 : 22'bz;  // Controlled_Buffer controlled_buffer_31
  assign OUT14_2 = decoder_2_out1 ? node_1_childrightout : 22'bz;  // Controlled_Buffer controlled_buffer_32
  assign controlled_buffer_31_out = decoder_2_out0 ? IN15_2 : 22'bz;  // Controlled_Buffer controlled_buffer_33
  assign OUT15_2 = decoder_2_out0 ? node_1_childrightout : 22'bz;  // Controlled_Buffer controlled_buffer_34
  assign controlled_buffer_31_out = decoder_2_out3 ? IN12_2 : 22'bz;  // Controlled_Buffer controlled_buffer_35
  assign OUT12_2 = decoder_2_out3 ? node_1_childrightout : 22'bz;  // Controlled_Buffer controlled_buffer_36
  assign controlled_buffer_31_out = decoder_2_out2 ? IN13_2 : 22'bz;  // Controlled_Buffer controlled_buffer_37
  assign OUT13_2 = decoder_2_out2 ? node_1_childrightout : 22'bz;  // Controlled_Buffer controlled_buffer_38
  assign controlled_buffer_31_out = decoder_2_out5 ? IN10_2 : 22'bz;  // Controlled_Buffer controlled_buffer_39
  assign OUT10_2 = decoder_2_out5 ? node_1_childrightout : 22'bz;  // Controlled_Buffer controlled_buffer_40
  assign controlled_buffer_31_out = decoder_2_out4 ? IN11_2 : 22'bz;  // Controlled_Buffer controlled_buffer_41
  assign OUT11_2 = decoder_2_out4 ? node_1_childrightout : 22'bz;  // Controlled_Buffer controlled_buffer_42
  Decoder #(.select(4)) decoder_2 (
    .out0(decoder_2_out0), .out1(decoder_2_out1), .out2(decoder_2_out2), .out3(decoder_2_out3),
    .out4(decoder_2_out4), .out5(decoder_2_out5), .out6(decoder_2_out6), .out7(decoder_2_out7),
    .out8(decoder_2_out8), .out9(decoder_2_out9), .out10(decoder_2_out10), .out11(decoder_2_out11),
    .out12(decoder_2_out12), .out13(decoder_2_out13), .out14(decoder_2_out14), .out15(decoder_2_out15),
    .sel(node_1_childrightpointerout));  // open: en
  assign controlled_buffer_31_out = decoder_2_out7 ? IN8_2 : 22'bz;  // Controlled_Buffer controlled_buffer_43
  assign OUT8_2 = decoder_2_out7 ? node_1_childrightout : 22'bz;  // Controlled_Buffer controlled_buffer_44
  assign controlled_buffer_31_out = decoder_2_out6 ? IN9_2 : 22'bz;  // Controlled_Buffer controlled_buffer_45
  assign OUT9_2 = decoder_2_out6 ? node_1_childrightout : 22'bz;  // Controlled_Buffer controlled_buffer_46
  assign controlled_buffer_31_out = decoder_2_out9 ? IN6_2 : 22'bz;  // Controlled_Buffer controlled_buffer_47
  assign OUT6_2 = decoder_2_out9 ? node_1_childrightout : 22'bz;  // Controlled_Buffer controlled_buffer_48
  assign controlled_buffer_31_out = decoder_2_out8 ? IN7_2 : 22'bz;  // Controlled_Buffer controlled_buffer_49
  assign OUT7_2 = decoder_2_out8 ? node_1_childrightout : 22'bz;  // Controlled_Buffer controlled_buffer_50
  assign controlled_buffer_31_out = decoder_2_out11 ? IN4_2 : 22'bz;  // Controlled_Buffer controlled_buffer_51
  assign OUT4_2 = decoder_2_out11 ? node_1_childrightout : 22'bz;  // Controlled_Buffer controlled_buffer_52
  assign controlled_buffer_31_out = decoder_2_out10 ? IN5_2 : 22'bz;  // Controlled_Buffer controlled_buffer_53
  assign OUT5_2 = decoder_2_out10 ? node_1_childrightout : 22'bz;  // Controlled_Buffer controlled_buffer_54
  assign controlled_buffer_31_out = decoder_2_out13 ? IN2_2 : 22'bz;  // Controlled_Buffer controlled_buffer_55
  assign OUT2_2 = decoder_2_out13 ? node_1_childrightout : 22'bz;  // Controlled_Buffer controlled_buffer_56
  assign controlled_buffer_31_out = decoder_2_out12 ? IN3_2 : 22'bz;  // Controlled_Buffer controlled_buffer_57
  assign OUT3_2 = decoder_2_out12 ? node_1_childrightout : 22'bz;  // Controlled_Buffer controlled_buffer_58
  assign controlled_buffer_31_out = decoder_2_out14 ? IN1_2 : 22'bz;  // Controlled_Buffer controlled_buffer_59
  assign OUT1_2 = decoder_2_out14 ? node_1_childrightout : 22'bz;  // Controlled_Buffer controlled_buffer_60
endmodule

module Node (
  input  NewNodeReturn,
  input  [21:0] ParentIn,
  input  [3:0] NewID,
  input  [21:0] ChildLeftIn,
  input  [21:0] ChildRightIn,
  input  Clock,
  input  [3:0] UniqueNodeID,
  output CurrentResolveState,
  output NewNodeRequest,
  output [2:0] CurrentExpressionType,
  output [21:0] ParentOut,
  output [21:0] ChildLeftOut,
  output [21:0] ChildRightOut,
  output [3:0] ChildRightPointerOut,
  output [3:0] ChildLeftPointerOut
);

  wire and_1_out, and_3_out, and_4_out, and_6_out, and_7_out, and_8_out, and_9_out, d_ff_1_q, d_ff_2_q,
       d_ff_3_q, functionexpression_1_resolveflagoveride, nameexpression_1_backstack,
       nameexpression_1_bufferwrite, nameexpression_1_clearchidlren, nameexpression_1_expwrite,
       nameexpression_1_frontstack, nameexpression_1_nametogglechildren, nameexpression_1_ramselect,
       nameexpression_1_ramwrite, nameexpression_1_stackclear, not_1_out, not_2_out, not_4_out, not_8_out,
       not_9_out, or_1_out, or_2_out, or_3_out, or_4_out, or_6_out;
  wire [2:0] nameexpression_1_newnode_2_3, not_3_out, not_5_out, not_6_out, not_7_out, register_4_q,
       xor_1_out, xor_2_out, xor_3_out, xor_4_out;
  wire [3:0] ChildL, ChildR, controlled_buffer_3_out, nameexpression_1_newnode_2,
       nameexpression_1_newnode_2_2, NewNode, ram_1_dout, register_5_q, register_6_q;
  wire [7:0] nameexpression_1_generaloutput;
  wire [11:0] functionexpression_1_newnode_2;
  wire [11:11] nameexpression_1_newnode_2_4;

  Register #(.width(4)) register_1 (
    .D(nameexpression_1_newnode_2), .en(nameexpression_1_expwrite), .clk(Clock), .Q(ChildR),
    .clr(nameexpression_1_clearchidlren));
  Register #(.width(4)) register_2 (
    .D(nameexpression_1_newnode_2_2), .en(nameexpression_1_expwrite), .clk(Clock), .Q(ChildL),
    .clr(nameexpression_1_clearchidlren));
  Register #(.width(3)) register_3 (
    .D(nameexpression_1_newnode_2_3), .en(nameexpression_1_expwrite), .clk(Clock), .Q(CurrentExpressionType));  // open: clr
  and and_1 (and_1_out, nameexpression_1_expwrite, nameexpression_1_newnode_2_4[11]);
  not not_1 (not_1_out, nameexpression_1_expwrite);
  and and_2 (and_1_out, not_1_out, and_3_out);
  and and_3 (and_3_out, functionexpression_1_resolveflagoveride, or_3_out);
  assign ChildLeftPointerOut = not_2_out ? ChildL : 4'bz;  // Controlled_Buffer controlled_buffer_1
  not not_2 (not_2_out, or_6_out);
  assign ChildLeftPointerOut = or_6_out ? 4'b0000 : 4'bz;  // Controlled_Buffer controlled_buffer_2
  assign xor_1_out = 3'b011 ^ CurrentExpressionType;  // XOR_Gate xor_1, 3 bits wide
  assign not_3_out = ~xor_1_out;  // NOT_Gate not_3, 3 bits wide
  D_Flip_Flop d_ff_1 (.D(or_1_out), .clk(Clock), .Q(d_ff_1_q));  // open: Qn, preset, reset
  or or_1 (or_1_out, and_6_out, and_1_out);
  or or_2 (or_2_out, d_ff_2_q, nameexpression_1_nametogglechildren);
  and and_4 (and_4_out, not_3_out[0], not_3_out[1], not_3_out[2]);
  and and_5 (CurrentResolveState, d_ff_1_q, or_3_out);
  D_Flip_Flop d_ff_2 (
    .D(or_2_out), .clk(Clock), .Q(d_ff_2_q), .reset(nameexpression_1_stackclear));  // open: Qn, preset
  Register #(.width(3)) register_4 (
    .D(nameexpression_1_generaloutput[2:0]), .en(nameexpression_1_bufferwrite), .clk(Clock), .Q(register_4_q));  // open: clr
  or or_3 (or_3_out, ChildLeftIn[20], ChildRightIn[20]);
  or or_4 (or_4_out, and_4_out, ParentIn[21]);
  D_Flip_Flop d_ff_3 (.D(ParentIn[21]), .clk(Clock), .Q(d_ff_3_q));  // open: Qn, preset, reset
  or or_5 (ChildRightOut[21], or_4_out, d_ff_3_q);
  assign xor_2_out = 3'b001 ^ CurrentExpressionType;  // XOR_Gate xor_2, 3 bits wide
  and and_6 (and_6_out, not_5_out[0], not_5_out[1], not_5_out[2]);
  not not_4 (not_4_out, d_ff_2_q);
  and and_7 (and_7_out, not_4_out, and_9_out);
  or or_6 (or_6_out, and_7_out, and_8_out);
  assign not_5_out = ~xor_2_out;  // NOT_Gate not_5, 3 bits wide
  NameExpression nameexpression_1 (
    .PEB(ParentIn[11:0]), .PIB(ParentIn[19:12]), .CRE(ChildRightIn[11:0]), .CRI(ChildRightIn[19:12]),
    .CLE(ChildLeftIn[11:0]), .CLI(ChildLeftIn[19:12]), .SFS(register_5_q), .SBS(register_6_q),
    .RAM(ram_1_dout), .InternalExpression({CurrentResolveState, CurrentExpressionType, ChildL, ChildR}),
    .Buffer(register_4_q), .EXPWrite(nameexpression_1_expwrite), .RamSelect(nameexpression_1_ramselect),
    .FrontStack(nameexpression_1_frontstack), .BackStack(nameexpression_1_backstack),
    .RAMwrite(nameexpression_1_ramwrite), .NewNode(NewNodeRequest), .Clock(Clock), .NewNodeID(NewNode),
    .UniqueNodeID(UniqueNodeID), .BufferWrite(nameexpression_1_bufferwrite),
    .NameToggleChildren(nameexpression_1_nametogglechildren), .ClearChidlren(nameexpression_1_clearchidlren),
    .StackClear(nameexpression_1_stackclear), .PEB_2(ParentOut[11:0]), .PIB_2(ParentOut[19:12]),
    .CRE_2(ChildRightOut[11:0]), .CRI_2(ChildRightOut[19:12]), .CLE_2(ChildLeftOut[11:0]),
    .CLI_2(ChildLeftOut[19:12]),
    .NewNode_2({nameexpression_1_newnode_2_4[11], nameexpression_1_newnode_2_3, nameexpression_1_newnode_2_2, nameexpression_1_newnode_2}),
    .GeneralOutput(nameexpression_1_generaloutput));
  and and_8 (and_8_out, not_6_out[0], not_6_out[1], not_6_out[2]);
  and and_9 (and_9_out, not_7_out[0], not_7_out[1], not_7_out[2]);
  assign not_6_out = ~xor_3_out;  // NOT_Gate not_6, 3 bits wide
  assign xor_3_out = CurrentExpressionType ^ 3'b100;  // XOR_Gate xor_3, 3 bits wide
  assign not_7_out = ~xor_4_out;  // NOT_Gate not_7, 3 bits wide
  assign xor_4_out = CurrentExpressionType ^ 3'b001;  // XOR_Gate xor_4, 3 bits wide
  UndefinedExpression undefinedexpression_1 (
    .PEB(ParentIn[11:0]), .PIB(ParentIn[19:12]), .CRE(ChildRightIn[11:0]), .CRI(ChildRightIn[19:12]),
    .CLE(ChildLeftIn[11:0]), .CLI(ChildLeftIn[19:12]), .SFS(ram_1_dout), .SBS(register_6_q),
    .RAM(ram_1_dout), .InternalExpression({CurrentResolveState, CurrentExpressionType, ChildL, ChildR}),
    .Buffer(register_4_q), .EXPWrite(nameexpression_1_expwrite), .RamSelect(nameexpression_1_ramselect),
    .FrontStack(nameexpression_1_frontstack), .BackStack(nameexpression_1_backstack),
    .RAMwrite(nameexpression_1_ramwrite), .NewNode(NewNodeRequest), .Clock(Clock), .NewNodeID(NewNode),
    .UniqueNodeID(UniqueNodeID), .ClearChidlren(nameexpression_1_clearchidlren),
    .StackClear(nameexpression_1_stackclear), .PEB_2(ParentOut[11:0]), .PIB_2(ParentOut[19:12]),
    .CRE_2(ChildRightOut[11:0]), .CRI_2(ChildRightOut[19:12]), .CLE_2(ChildLeftOut[11:0]),
    .CLI_2(ChildLeftOut[19:12]),
    .NewNode_2({nameexpression_1_newnode_2_4[11], nameexpression_1_newnode_2_3, nameexpression_1_newnode_2_2, nameexpression_1_newnode_2}),
    .GeneralOutput(nameexpression_1_generaloutput));
  GoToExpression gotoexpression_1 (
    .PEB(ParentIn[11:0]), .PIB(ParentIn[19:12]), .CRE(ChildRightIn[11:0]), .CRI(ChildRightIn[19:12]),
    .CLE(ChildLeftIn[11:0]), .CLI(ChildLeftIn[19:12]), .SFS(ram_1_dout), .SBS(register_6_q),
    .RAM(ram_1_dout), .InternalExpression({CurrentResolveState, CurrentExpressionType, ChildL, ChildR}),
    .Buffer(register_4_q), .EXPWrite(nameexpression_1_expwrite), .RamSelect(nameexpression_1_ramselect),
    .FrontStack(nameexpression_1_frontstack), .BackStack(nameexpression_1_backstack),
    .RAMwrite(nameexpression_1_ramwrite), .NewNode(NewNodeRequest), .Clock(Clock), .NewNodeID(NewNode),
    .UniqueNodeID(UniqueNodeID), .ClearChidlren(nameexpression_1_clearchidlren),
    .StackClear(nameexpression_1_stackclear), .PEB_2(ParentOut[11:0]), .PIB_2(ParentOut[19:12]),
    .CRE_2(ChildRightOut[11:0]), .CRI_2(ChildRightOut[19:12]), .CLE_2(ChildLeftOut[11:0]),
    .CLI_2(ChildLeftOut[19:12]),
    .NewNode_2({nameexpression_1_newnode_2_4[11], nameexpression_1_newnode_2_3, nameexpression_1_newnode_2_2, nameexpression_1_newnode_2}),
    .GeneralOutput(nameexpression_1_generaloutput));
  ApplicationExpression applicationexpression_1 (
    .PEB(ParentIn[11:0]), .PIB(ParentIn[19:12]), .CRE(ChildRightIn[11:0]), .CRI(ChildRightIn[19:12]),
    .CLE(ChildLeftIn[11:0]), .CLI(ChildLeftIn[19:12]), .SFS(ram_1_dout), .SBS(register_6_q),
    .RAM(ram_1_dout), .InternalExpression({CurrentResolveState, CurrentExpressionType, ChildL, ChildR}),
    .Buffer(register_4_q), .EXPWrite(nameexpression_1_expwrite), .RamSelect(nameexpression_1_ramselect),
    .FrontStack(nameexpression_1_frontstack), .BackStack(nameexpression_1_backstack),
    .RAMwrite(nameexpression_1_ramwrite), .NewNode(NewNodeRequest), .Clock(Clock), .NewNodeID(NewNode),
    .UniqueNodeID(UniqueNodeID), .ClearChidlren(nameexpression_1_clearchidlren),
    .StackClear(nameexpression_1_stackclear), .PEB_2(ParentOut[11:0]), .PIB_2(ParentOut[19:12]),
    .CRE_2(ChildRightOut[11:0]), .CRI_2(ChildRightOut[19:12]), .CLE_2(ChildLeftOut[11:0]),
    .CLI_2(ChildLeftOut[19:12]),
    .NewNode_2({nameexpression_1_newnode_2_4[11], nameexpression_1_newnode_2_3, nameexpression_1_newnode_2_2, nameexpression_1_newnode_2}),
    .GeneralOutput(nameexpression_1_generaloutput));
  FunctionExpression functionexpression_1 (
    .PEB(ParentIn[11:0]), .PIB(ParentIn[19:12]), .CRE(ChildRightIn[11:0]), .CRI(ChildRightIn[19:12]),
    .CLE(ChildLeftIn[11:0]), .CLI(ChildLeftIn[19:12]), .SFS(ram_1_dout), .SBS(register_6_q),
    .RAM(ram_1_dout), .InternalExpression({CurrentResolveState, CurrentExpressionType, ChildL, ChildR}),
    .UnreduceFlag(d_ff_3_q), .EXPWrite(nameexpression_1_expwrite), .RamSelect(nameexpression_1_ramselect),
    .FrontStack(nameexpression_1_frontstack), .BackStack(nameexpression_1_backstack),
    .RAMwrite(nameexpression_1_ramwrite), .NewNode(NewNodeRequest), .Clock(Clock), .NewNodeID(NewNode),
    .UniqueNodeID(UniqueNodeID), .ResolveFlagOveride(functionexpression_1_resolveflagoveride),
    .ClearChidlren(nameexpression_1_clearchidlren), .StackClear(nameexpression_1_stackclear),
    .PEB_2(ParentOut[11:0]), .PIB_2(ParentOut[19:12]), .CRE_2(ChildRightOut[11:0]),
    .CRI_2(ChildRightOut[19:12]), .CLE_2(ChildLeftOut[11:0]), .CLI_2(ChildLeftOut[19:12]),
    .NewNode_2(functionexpression_1_newnode_2), .GeneralOutput(nameexpression_1_generaloutput));
  Register #(.width(4)) register_5 (
    .D(nameexpression_1_generaloutput[3:0]), .en(nameexpression_1_frontstack), .clk(Clock), .Q(register_5_q),
    .clr(nameexpression_1_stackclear));
  RAM #(.addrWidth(4), .dataWidth(4), .databus("bibus")) ram_1 (
    .addr(controlled_buffer_3_out), .we(nameexpression_1_ramwrite), .oe(1'b1), .clk(Clock),
    .din(nameexpression_1_generaloutput[3:0]), .dout(ram_1_dout));
  not not_8 (not_8_out, and_7_out);
  Register #(.width(4)) NewNodeID (.D(NewID), .en(NewNodeRequest), .clk(NewNodeReturn), .Q(NewNode));  // open: clr
  assign controlled_buffer_3_out = nameexpression_1_ramselect ? register_5_q : 4'bz;  // Controlled_Buffer controlled_buffer_3
  assign ChildRightPointerOut = not_8_out ? ChildR : 4'bz;  // Controlled_Buffer controlled_buffer_4
  assign ChildRightPointerOut = and_7_out ? 4'b0000 : 4'bz;  // Controlled_Buffer controlled_buffer_5
  Register #(.width(4)) register_6 (
    .D(nameexpression_1_generaloutput[3:0]), .en(nameexpression_1_backstack), .clk(Clock), .Q(register_6_q),
    .clr(nameexpression_1_stackclear));
  assign controlled_buffer_3_out = not_9_out ? register_6_q : 4'bz;  // Controlled_Buffer controlled_buffer_6
  not not_9 (not_9_out, nameexpression_1_ramselect);

  assign ChildLeftOut[21:20] = 2'b00;
  assign ChildRightOut[20] = 1'b0;
  assign ParentOut[21:20] = {ChildRightOut[21], CurrentResolveState};

  // Other names for the same wires on the sheet: Expres[2:0] = CurrentExpressionType

  // Notes on the sheet:
  //   Resolve Flag
  //   Reduce Flag
  //   FrontStack
  //   BackStack
endmodule

module UndefinedExpression (
  input  [11:0] PEB,
  input  [7:0] PIB,
  input  [11:0] CRE,
  input  [7:0] CRI,
  input  [11:0] CLE,
  input  [7:0] CLI,
  input  [3:0] SFS,
  input  [3:0] SBS,
  input  [3:0] RAM,
  input  [11:0] InternalExpression,
  input  [2:0] Buffer,
  input  Clock,
  input  [3:0] NewNodeID,
  input  [3:0] UniqueNodeID,
  output EXPWrite,
  output RamSelect,
  output FrontStack,
  output BackStack,
  output RAMwrite,
  output NewNode,
  output [11:0] PEB_2,
  output [7:0] PIB_2,
  output [11:0] CRE_2,
  output [7:0] CRI_2,
  output [11:0] CLE_2,
  output [7:0] CLI_2,
  output [11:0] NewNode_2,
  output [7:0] GeneralOutput,
  output ClearChidlren,
  output StackClear
);

  wire and_1_out, decoder_1_out2, decoder_1_out3, decoder_1_out4, not_2_out, not_3_out, not_4_out, not_5_out,
       not_6_out, or_1_out, or_2_out, or_3_out, or_4_out, or_5_out, or_6_out, or_7_out, or_8_out, or_9_out,
       or_10_out, or_11_out, or_12_out, or_13_out, or_14_out, or_15_out, updateexpression_1_updcle,
       updateexpression_1_updcli, updateexpression_1_updcre, updateexpression_1_updcri,
       updateexpression_1_updexp, updateexpression_1_updstackclear, updatepointerleft_1_updcle,
       updatepointerleft_1_updcli, updatepointerleft_1_updcre, updatepointerleft_1_updcri,
       updatepointerleft_1_updexp, updatepointerright_1_updcle, updatepointerright_1_updcli,
       updatepointerright_1_updcre, updatepointerright_1_updcri, updatepointerright_1_updexp;
  wire [2:0] not_1_out, xor_1_out;
  wire [7:0] controlled_buffer_2_out, controlled_buffer_4_out, updateexpression_1_cli,
       updateexpression_1_cri, updatepointerleft_1_cli, updatepointerleft_1_cri, updatepointerright_1_cli,
       updatepointerright_1_cri;
  wire [11:0] controlled_buffer_1_out, controlled_buffer_3_out, controlled_buffer_5_out,
       updateexpression_1_cle, updateexpression_1_cre, updateexpression_1_newvalue, updatepointerleft_1_cle,
       updatepointerleft_1_cre, updatepointerleft_1_newvalue, updatepointerright_1_cli_2,
       updatepointerright_1_cri_2, updatepointerright_1_newvalue;

  Decoder #(.select(4)) decoder_1 (
    .out2(decoder_1_out2), .out3(decoder_1_out3), .out4(decoder_1_out4), .sel(PIB[7:4]));  // open: out0, out1, out5, out6, out7, out8, out9, out10, out11, out12, out13, out14, out15, en
  assign xor_1_out = InternalExpression[10:8] ^ 3'b000;  // XOR_Gate xor_1, 3 bits wide
  assign controlled_buffer_1_out = updateexpression_1_updcre ? updateexpression_1_cre : 12'bz;  // Controlled_Buffer controlled_buffer_1
  buf or_1 (or_1_out, updateexpression_1_updcri);  // OR_Gate
  assign controlled_buffer_2_out = updateexpression_1_updcri ? updateexpression_1_cri : 8'bz;  // Controlled_Buffer controlled_buffer_2
  UpdateExpression updateexpression_1 (
    .ActivationSignal(decoder_1_out2), .Clock(Clock), .UniqueNodeID(UniqueNodeID), .PIB(PIB), .PEB(PEB),
    .UpdCLE(updateexpression_1_updcle), .UpdCRE(updateexpression_1_updcre),
    .UpdCLI(updateexpression_1_updcli), .UpdCRI(updateexpression_1_updcri),
    .UpdStackClear(updateexpression_1_updstackclear), .UpdEXP(updateexpression_1_updexp),
    .CRI(updateexpression_1_cri), .CLI(updateexpression_1_cli), .CRE(updateexpression_1_cre),
    .CLE(updateexpression_1_cle), .NewValue(updateexpression_1_newvalue));
  assign not_1_out = ~xor_1_out;  // NOT_Gate not_1, 3 bits wide
  assign controlled_buffer_3_out = updateexpression_1_updcle ? updateexpression_1_cle : 12'bz;  // Controlled_Buffer controlled_buffer_3
  buf or_2 (or_2_out, updateexpression_1_updcli);  // OR_Gate
  assign controlled_buffer_4_out = updateexpression_1_updcli ? updateexpression_1_cli : 8'bz;  // Controlled_Buffer controlled_buffer_4
  buf or_3 (or_3_out, updateexpression_1_updexp);  // OR_Gate
  assign controlled_buffer_5_out = updateexpression_1_updexp ? updateexpression_1_newvalue : 12'bz;  // Controlled_Buffer controlled_buffer_5
  and and_1 (and_1_out, not_1_out[0], not_1_out[1], not_1_out[2]);
  or or_4 (or_4_out, updateexpression_1_updexp, updatepointerleft_1_updexp);
  assign controlled_buffer_1_out = updatepointerleft_1_updcre ? updatepointerleft_1_cre : 12'bz;  // Controlled_Buffer controlled_buffer_6
  UpdatePointerLeft updatepointerleft_1 (
    .ActivationSignal(decoder_1_out3), .Clock(Clock), .UniqueNodeID(UniqueNodeID), .PIB(PIB),
    .InternalExpression(InternalExpression), .PEB(PEB), .UpdCLE(updatepointerleft_1_updcle),
    .UpdCRE(updatepointerleft_1_updcre), .UpdCLI(updatepointerleft_1_updcli),
    .UpdCRI(updatepointerleft_1_updcri), .UpdEXP(updatepointerleft_1_updexp), .CRI(updatepointerleft_1_cri),
    .CLI(updatepointerleft_1_cli), .CRE(updatepointerleft_1_cre), .CLE(updatepointerleft_1_cle),
    .NewValue(updatepointerleft_1_newvalue));
  or or_5 (or_5_out, updateexpression_1_updcre, updatepointerleft_1_updcre);
  or or_6 (or_6_out, or_1_out, updatepointerleft_1_updcri);
  assign controlled_buffer_2_out = updatepointerleft_1_updcri ? updatepointerleft_1_cri : 8'bz;  // Controlled_Buffer controlled_buffer_7
  or or_7 (or_7_out, updateexpression_1_updcle, updatepointerleft_1_updcle);
  assign controlled_buffer_3_out = updatepointerleft_1_updcle ? updatepointerleft_1_cle : 12'bz;  // Controlled_Buffer controlled_buffer_8
  or or_8 (or_8_out, or_2_out, updatepointerleft_1_updcli);
  assign controlled_buffer_4_out = updatepointerleft_1_updcli ? updatepointerleft_1_cli : 8'bz;  // Controlled_Buffer controlled_buffer_9
  or or_9 (or_9_out, or_3_out, updatepointerleft_1_updexp);
  assign controlled_buffer_5_out = updatepointerleft_1_updexp ? updatepointerleft_1_newvalue : 12'bz;  // Controlled_Buffer controlled_buffer_10
  UpdatePointerRight updatepointerright_1 (
    .ActivationSignal(decoder_1_out4), .Clock(Clock), .UniqueNodeID(UniqueNodeID), .PIB(PIB),
    .InternalExpression(InternalExpression), .PEB(PEB), .UpdCLE(updatepointerright_1_updcle),
    .UpdCRE(updatepointerright_1_updcre), .UpdCLI(updatepointerright_1_updcli),
    .UpdCRI(updatepointerright_1_updcri), .UpdEXP(updatepointerright_1_updexp),
    .CRI(updatepointerright_1_cri), .CLI(updatepointerright_1_cli), .CRI_2(updatepointerright_1_cri_2),
    .CLI_2(updatepointerright_1_cli_2), .NewValue(updatepointerright_1_newvalue));
  or or_10 (or_10_out, or_4_out, updatepointerright_1_updexp);
  or or_11 (or_11_out, or_5_out, updatepointerright_1_updcre);
  assign controlled_buffer_1_out = updatepointerright_1_updcre ? updatepointerright_1_cri_2 : 12'bz;  // Controlled_Buffer controlled_buffer_11
  or or_12 (or_12_out, or_6_out, updatepointerright_1_updcri);
  assign controlled_buffer_2_out = updatepointerright_1_updcri ? updatepointerright_1_cri : 8'bz;  // Controlled_Buffer controlled_buffer_12
  or or_13 (or_13_out, or_7_out, updatepointerright_1_updcle);
  assign controlled_buffer_3_out = updatepointerright_1_updcle ? updatepointerright_1_cli_2 : 12'bz;  // Controlled_Buffer controlled_buffer_13
  or or_14 (or_14_out, or_8_out, updatepointerright_1_updcli);
  assign controlled_buffer_4_out = updatepointerright_1_updcli ? updatepointerright_1_cli : 8'bz;  // Controlled_Buffer controlled_buffer_14
  or or_15 (or_15_out, or_9_out, updatepointerright_1_updexp);
  assign controlled_buffer_5_out = updatepointerright_1_updexp ? updatepointerright_1_newvalue : 12'bz;  // Controlled_Buffer controlled_buffer_15
  assign RamSelect = and_1_out ? 1'b0 : 1'bz;  // Controlled_Buffer controlled_buffer_16
  assign BackStack = and_1_out ? 1'b0 : 1'bz;  // Controlled_Buffer controlled_buffer_17
  assign FrontStack = and_1_out ? 1'b0 : 1'bz;  // Controlled_Buffer controlled_buffer_18
  assign RAMwrite = and_1_out ? 1'b0 : 1'bz;  // Controlled_Buffer controlled_buffer_19
  assign EXPWrite = and_1_out ? or_10_out : 1'bz;  // Controlled_Buffer controlled_buffer_20
  assign NewNode = and_1_out ? 1'b0 : 1'bz;  // Controlled_Buffer controlled_buffer_21
  not not_2 (not_2_out, or_11_out);
  assign controlled_buffer_1_out = not_2_out ? {12{1'b0}} : 12'bz;  // Controlled_Buffer controlled_buffer_22
  not not_3 (not_3_out, or_12_out);
  assign controlled_buffer_2_out = not_3_out ? {8{1'b0}} : 8'bz;  // Controlled_Buffer controlled_buffer_23
  not not_4 (not_4_out, or_13_out);
  assign controlled_buffer_3_out = not_4_out ? {12{1'b0}} : 12'bz;  // Controlled_Buffer controlled_buffer_24
  not not_5 (not_5_out, or_14_out);
  assign controlled_buffer_4_out = not_5_out ? {8{1'b0}} : 8'bz;  // Controlled_Buffer controlled_buffer_25
  not not_6 (not_6_out, or_15_out);
  assign controlled_buffer_5_out = not_6_out ? {12{1'b0}} : 12'bz;  // Controlled_Buffer controlled_buffer_26
  assign ClearChidlren = and_1_out ? 1'b0 : 1'bz;  // Controlled_Buffer controlled_buffer_27
  assign PEB_2 = and_1_out ? {12{1'b0}} : 12'bz;  // Controlled_Buffer controlled_buffer_28
  assign PIB_2 = and_1_out ? {8{1'b0}} : 8'bz;  // Controlled_Buffer controlled_buffer_29
  assign CRE_2 = and_1_out ? controlled_buffer_1_out : 12'bz;  // Controlled_Buffer controlled_buffer_30
  assign CRI_2 = and_1_out ? controlled_buffer_2_out : 8'bz;  // Controlled_Buffer controlled_buffer_31
  assign CLE_2 = and_1_out ? controlled_buffer_3_out : 12'bz;  // Controlled_Buffer controlled_buffer_32
  assign CLI_2 = and_1_out ? controlled_buffer_4_out : 8'bz;  // Controlled_Buffer controlled_buffer_33
  assign NewNode_2 = and_1_out ? controlled_buffer_5_out : 12'bz;  // Controlled_Buffer controlled_buffer_34
  assign GeneralOutput = and_1_out ? {8{1'b0}} : 8'bz;  // Controlled_Buffer controlled_buffer_35
  assign StackClear = and_1_out ? updateexpression_1_updstackclear : 1'bz;  // Controlled_Buffer controlled_buffer_36

  // Notes on the sheet:
  //   Input
  //   0 == Backstack / 1 == Frontstack
  //   Output
endmodule

module NameExpression (
  input  [11:0] PEB,
  input  [7:0] PIB,
  input  [11:0] CRE,
  input  [7:0] CRI,
  input  [11:0] CLE,
  input  [7:0] CLI,
  input  [3:0] SFS,
  input  [3:0] SBS,
  input  [3:0] RAM,
  input  [11:0] InternalExpression,
  input  [2:0] Buffer,
  input  Clock,
  input  [3:0] NewNodeID,
  input  [3:0] UniqueNodeID,
  output EXPWrite,
  output RamSelect,
  output FrontStack,
  output BackStack,
  output RAMwrite,
  output NewNode,
  output [11:0] PEB_2,
  output [7:0] PIB_2,
  output [11:0] CRE_2,
  output [7:0] CRI_2,
  output [11:0] CLE_2,
  output [7:0] CLI_2,
  output [11:0] NewNode_2,
  output [7:0] GeneralOutput,
  output BufferWrite,
  output NameToggleChildren,
  output ClearChidlren,
  output StackClear
);

  wire and_1_out, comparevalue_1_comcle, comparevalue_1_comcli, comparevalue_1_comcre, comparevalue_1_comcri,
       comparevalue_1_compib, comparevalue_1_markfortransformation, decoder_1_out1, decoder_1_out2,
       decoder_1_out3, decoder_1_out4, decoder_1_out5, decoder_1_out6, decoder_1_out7, decoder_1_out8,
       decoder_1_out9, immediateresolution_1_immpib, not_2_out, not_3_out, not_4_out, not_5_out, not_6_out,
       not_7_out, not_8_out, not_9_out, nullification_1_nullcli, nullification_1_nullcri,
       nullification_1_nullexp, nullification_1_nullstackclear, or_1_out, or_2_out, or_3_out, or_4_out,
       or_5_out, or_6_out, or_7_out, or_8_out, or_9_out, or_10_out, or_11_out, or_12_out, or_13_out,
       or_14_out, or_15_out, or_16_out, or_17_out, or_18_out, or_19_out, or_20_out, or_21_out, or_22_out,
       or_23_out, or_24_out, or_25_out, or_26_out, or_27_out, or_28_out, or_29_out, or_30_out, or_31_out,
       or_32_out, or_33_out, or_34_out, or_35_out, or_36_out, or_37_out, or_38_out, or_39_out, or_40_out,
       or_41_out, or_42_out, or_43_out, or_44_out, or_45_out,
       preparefortransformationasancestorinput_1_ptacli, preparefortransformationasancestorinput_1_ptacri,
       preparefortransformationasancestorinput_1_ptapeb, preparefortransformationasancestorinput_1_ptapib,
       preparefortransformationasancestorinput_1_ptaram, preparefortransformationasancestorinput_1_ptasbs,
       preparefortransformationasancestorinput_1_ptasel, preparefortransformationasancestorinput_1_ptasfs,
       preparefortransformationasancestorinput_1_ptastackclear,
       preparefortransformationasdecendantinput_1_ptdclc, preparefortransformationasdecendantinput_1_ptdcle,
       preparefortransformationasdecendantinput_1_ptdcli,
       preparefortransformationasdecendantinput_1_ptdcomparevalueclear,
       preparefortransformationasdecendantinput_1_ptdcre, preparefortransformationasdecendantinput_1_ptdcri,
       preparefortransformationasdecendantinput_1_ptdexp, preparefortransformationasdecendantinput_1_ptdnew,
       preparefortransformationasdecendantinput_1_ptdpib, preparefortransformationasdecendantinput_1_ptdram,
       preparefortransformationasdecendantinput_1_ptdsbs, preparefortransformationasdecendantinput_1_ptdsel,
       preparefortransformationasdecendantinput_1_ptdsfs,
       preparefortransformationasdecendantinput_1_ptdstackclear, returnexpression_1_retcli,
       returnexpression_1_retcri, returnexpression_1_retpeb, returnexpression_1_retpib,
       updateexpression_1_updcle, updateexpression_1_updcli, updateexpression_1_updcre,
       updateexpression_1_updcri, updateexpression_1_updexp, updateexpression_1_updstackclear,
       updatepointerleft_1_updcle, updatepointerleft_1_updcli, updatepointerleft_1_updcre,
       updatepointerleft_1_updcri, updatepointerleft_1_updexp, updatepointerright_1_updcle,
       updatepointerright_1_updcli, updatepointerright_1_updcre, updatepointerright_1_updcri,
       updatepointerright_1_updexp;
  wire [2:0] not_1_out, xor_1_out;
  wire [7:0] comparevalue_1_cli_2, comparevalue_1_cri_2, comparevalue_1_pib_2, controlled_buffer_1_out,
       controlled_buffer_2_out, controlled_buffer_20_out, controlled_buffer_33_out,
       immediateresolution_1_out_3, nullification_1_cli, nullification_1_cri,
       preparefortransformationasancestorinput_1_cli_2, preparefortransformationasancestorinput_1_cri_2,
       preparefortransformationasancestorinput_1_generalouput, preparefortransformationasancestorinput_1_pib,
       preparefortransformationasdecendantinput_1_cli_2, preparefortransformationasdecendantinput_1_cri_2,
       preparefortransformationasdecendantinput_1_output, preparefortransformationasdecendantinput_1_pib_2,
       returnexpression_1_cli_2, returnexpression_1_cri_2, returnexpression_1_pib_2, updateexpression_1_cli,
       updateexpression_1_cri, updatepointerleft_1_cli, updatepointerleft_1_cri, updatepointerright_1_cli,
       updatepointerright_1_cri;
  wire [11:0] comparevalue_1_cle, comparevalue_1_cre, controlled_buffer_3_out, controlled_buffer_4_out,
       controlled_buffer_6_out, controlled_buffer_19_out, nullification_1_newvalue,
       preparefortransformationasancestorinput_1_peb, preparefortransformationasdecendantinput_1_cle,
       preparefortransformationasdecendantinput_1_cre,
       preparefortransformationasdecendantinput_1_newexpression, returnexpression_1_peb,
       updateexpression_1_cle, updateexpression_1_cre, updateexpression_1_newvalue, updatepointerleft_1_cle,
       updatepointerleft_1_cre, updatepointerleft_1_newvalue, updatepointerright_1_cli_2,
       updatepointerright_1_cri_2, updatepointerright_1_newvalue;

  Decoder #(.select(4)) decoder_1 (
    .out1(decoder_1_out1), .out2(decoder_1_out2), .out3(decoder_1_out3), .out4(decoder_1_out4),
    .out5(decoder_1_out5), .out6(decoder_1_out6), .out7(decoder_1_out7), .out8(decoder_1_out8),
    .out9(decoder_1_out9), .sel(PIB[7:4]));  // open: out0, out10, out11, out12, out13, out14, out15, en
  Nullification nullification_1 (
    .ActivationSignal(decoder_1_out1), .Clock(Clock), .NullCLI(nullification_1_nullcli),
    .NullCRI(nullification_1_nullcri), .NullStackClear(nullification_1_nullstackclear),
    .NullEXP(nullification_1_nullexp), .CRI(nullification_1_cri), .CLI(nullification_1_cli),
    .NewValue(nullification_1_newvalue));
  assign controlled_buffer_1_out = nullification_1_nullcli ? nullification_1_cri : 8'bz;  // Controlled_Buffer controlled_buffer_1
  assign controlled_buffer_2_out = nullification_1_nullcri ? nullification_1_cli : 8'bz;  // Controlled_Buffer controlled_buffer_2
  assign controlled_buffer_3_out = nullification_1_nullexp ? nullification_1_newvalue : 12'bz;  // Controlled_Buffer controlled_buffer_3
  UpdateExpression updateexpression_1 (
    .ActivationSignal(decoder_1_out2), .Clock(Clock), .UniqueNodeID(UniqueNodeID), .PIB(PIB), .PEB(PEB),
    .UpdCLE(updateexpression_1_updcle), .UpdCRE(updateexpression_1_updcre),
    .UpdCLI(updateexpression_1_updcli), .UpdCRI(updateexpression_1_updcri),
    .UpdStackClear(updateexpression_1_updstackclear), .UpdEXP(updateexpression_1_updexp),
    .CRI(updateexpression_1_cri), .CLI(updateexpression_1_cli), .CRE(updateexpression_1_cre),
    .CLE(updateexpression_1_cle), .NewValue(updateexpression_1_newvalue));
  assign not_1_out = ~xor_1_out;  // NOT_Gate not_1, 3 bits wide
  assign xor_1_out = InternalExpression[10:8] ^ 3'b001;  // XOR_Gate xor_1, 3 bits wide
  or or_1 (or_1_out, nullification_1_nullexp, updateexpression_1_updexp);
  assign controlled_buffer_4_out = updateexpression_1_updcre ? updateexpression_1_cre : 12'bz;  // Controlled_Buffer controlled_buffer_4
  or or_2 (or_2_out, nullification_1_nullcli, updateexpression_1_updcri);
  assign controlled_buffer_1_out = updateexpression_1_updcri ? updateexpression_1_cri : 8'bz;  // Controlled_Buffer controlled_buffer_5
  assign controlled_buffer_6_out = updateexpression_1_updcle ? updateexpression_1_cle : 12'bz;  // Controlled_Buffer controlled_buffer_6
  or or_3 (or_3_out, nullification_1_nullcri, updateexpression_1_updcli);
  assign controlled_buffer_2_out = updateexpression_1_updcli ? updateexpression_1_cli : 8'bz;  // Controlled_Buffer controlled_buffer_7
  or or_4 (or_4_out, nullification_1_nullexp, updateexpression_1_updexp);
  assign controlled_buffer_3_out = updateexpression_1_updexp ? updateexpression_1_newvalue : 12'bz;  // Controlled_Buffer controlled_buffer_8
  or or_5 (or_5_out, nullification_1_nullstackclear, updateexpression_1_updstackclear);
  and and_1 (and_1_out, not_1_out[0], not_1_out[1], not_1_out[2]);
  UpdatePointerLeft updatepointerleft_1 (
    .ActivationSignal(decoder_1_out3), .Clock(Clock), .UniqueNodeID(UniqueNodeID), .PIB(PIB),
    .InternalExpression(InternalExpression), .PEB(PEB), .UpdCLE(updatepointerleft_1_updcle),
    .UpdCRE(updatepointerleft_1_updcre), .UpdCLI(updatepointerleft_1_updcli),
    .UpdCRI(updatepointerleft_1_updcri), .UpdEXP(updatepointerleft_1_updexp), .CRI(updatepointerleft_1_cri),
    .CLI(updatepointerleft_1_cli), .CRE(updatepointerleft_1_cre), .CLE(updatepointerleft_1_cle),
    .NewValue(updatepointerleft_1_newvalue));
  or or_6 (or_6_out, or_1_out, updatepointerleft_1_updexp);
  or or_7 (or_7_out, updateexpression_1_updcre, updatepointerleft_1_updcre);
  assign controlled_buffer_4_out = updatepointerleft_1_updcre ? updatepointerleft_1_cre : 12'bz;  // Controlled_Buffer controlled_buffer_9
  or or_8 (or_8_out, or_2_out, updatepointerleft_1_updcri);
  assign controlled_buffer_1_out = updatepointerleft_1_updcri ? updatepointerleft_1_cri : 8'bz;  // Controlled_Buffer controlled_buffer_10
  or or_9 (or_9_out, updateexpression_1_updcle, updatepointerleft_1_updcle);
  assign controlled_buffer_6_out = updatepointerleft_1_updcle ? updatepointerleft_1_cle : 12'bz;  // Controlled_Buffer controlled_buffer_11
  or or_10 (or_10_out, or_3_out, updatepointerleft_1_updcli);
  assign controlled_buffer_2_out = updatepointerleft_1_updcli ? updatepointerleft_1_cli : 8'bz;  // Controlled_Buffer controlled_buffer_12
  or or_11 (or_11_out, or_4_out, updatepointerleft_1_updexp);
  assign controlled_buffer_3_out = updatepointerleft_1_updexp ? updatepointerleft_1_newvalue : 12'bz;  // Controlled_Buffer controlled_buffer_13
  UpdatePointerRight updatepointerright_1 (
    .ActivationSignal(decoder_1_out4), .Clock(Clock), .UniqueNodeID(UniqueNodeID), .PIB(PIB),
    .InternalExpression(InternalExpression), .PEB(PEB), .UpdCLE(updatepointerright_1_updcle),
    .UpdCRE(updatepointerright_1_updcre), .UpdCLI(updatepointerright_1_updcli),
    .UpdCRI(updatepointerright_1_updcri), .UpdEXP(updatepointerright_1_updexp),
    .CRI(updatepointerright_1_cri), .CLI(updatepointerright_1_cli), .CRI_2(updatepointerright_1_cri_2),
    .CLI_2(updatepointerright_1_cli_2), .NewValue(updatepointerright_1_newvalue));
  or or_12 (or_12_out, or_6_out, updatepointerright_1_updexp);
  or or_13 (or_13_out, or_7_out, updatepointerright_1_updcre);
  assign controlled_buffer_4_out = updatepointerright_1_updcre ? updatepointerright_1_cri_2 : 12'bz;  // Controlled_Buffer controlled_buffer_14
  or or_14 (or_14_out, or_8_out, updatepointerright_1_updcri);
  assign controlled_buffer_1_out = updatepointerright_1_updcri ? updatepointerright_1_cri : 8'bz;  // Controlled_Buffer controlled_buffer_15
  or or_15 (or_15_out, or_9_out, updatepointerright_1_updcle);
  assign controlled_buffer_6_out = updatepointerright_1_updcle ? updatepointerright_1_cli_2 : 12'bz;  // Controlled_Buffer controlled_buffer_16
  or or_16 (or_16_out, or_10_out, updatepointerright_1_updcli);
  assign controlled_buffer_2_out = updatepointerright_1_updcli ? updatepointerright_1_cli : 8'bz;  // Controlled_Buffer controlled_buffer_17
  or or_17 (or_17_out, or_11_out, updatepointerright_1_updexp);
  assign controlled_buffer_3_out = updatepointerright_1_updexp ? updatepointerright_1_newvalue : 12'bz;  // Controlled_Buffer controlled_buffer_18
  assign controlled_buffer_19_out = returnexpression_1_retpeb ? returnexpression_1_peb : 12'bz;  // Controlled_Buffer controlled_buffer_19
  assign controlled_buffer_20_out = returnexpression_1_retpib ? returnexpression_1_pib_2 : 8'bz;  // Controlled_Buffer controlled_buffer_20
  or or_18 (or_18_out, or_14_out, returnexpression_1_retcri);
  assign controlled_buffer_1_out = returnexpression_1_retcri ? returnexpression_1_cri_2 : 8'bz;  // Controlled_Buffer controlled_buffer_21
  ReturnExpression returnexpression_1 (
    .ActivationSignal(decoder_1_out5), .UniqueNodeID(UniqueNodeID), .PIB(PIB), .CLI(CLI), .CRI(CRI),
    .CRE(CRE), .CLE(CLE), .InternalExpression(InternalExpression), .RetCLI(returnexpression_1_retcli),
    .RetCRI(returnexpression_1_retcri), .RetPIB(returnexpression_1_retpib),
    .RetPEB(returnexpression_1_retpeb), .CRI_2(returnexpression_1_cri_2), .CLI_2(returnexpression_1_cli_2),
    .PEB(returnexpression_1_peb), .PIB_2(returnexpression_1_pib_2));
  or or_19 (or_19_out, or_16_out, returnexpression_1_retcli);
  assign controlled_buffer_2_out = returnexpression_1_retcli ? returnexpression_1_cli_2 : 8'bz;  // Controlled_Buffer controlled_buffer_22
  CompareValue comparevalue_1 (
    .ActivationSignal(decoder_1_out6), .Clock(Clock),
    .Clear(preparefortransformationasdecendantinput_1_ptdcomparevalueclear),
    .InternalValue(InternalExpression), .PEB(PEB), .PIB(PIB), .CRI(CRI), .CLI(CLI),
    .ComCLI(comparevalue_1_comcli), .ComCLE(comparevalue_1_comcle), .ComCRI(comparevalue_1_comcri),
    .ComCRE(comparevalue_1_comcre), .ComPIB(comparevalue_1_compib),
    .MarkForTransformation(comparevalue_1_markfortransformation), .CLI_2(comparevalue_1_cli_2),
    .CRI_2(comparevalue_1_cri_2), .CLE(comparevalue_1_cle), .CRE(comparevalue_1_cre),
    .PIB_2(comparevalue_1_pib_2));
  or or_20 (or_20_out, returnexpression_1_retpib, comparevalue_1_compib);
  assign controlled_buffer_20_out = comparevalue_1_compib ? comparevalue_1_pib_2 : 8'bz;  // Controlled_Buffer controlled_buffer_23
  or or_21 (or_21_out, or_13_out, comparevalue_1_comcre);
  assign controlled_buffer_4_out = comparevalue_1_comcre ? comparevalue_1_cre : 12'bz;  // Controlled_Buffer controlled_buffer_24
  or or_22 (or_22_out, or_18_out, comparevalue_1_comcri);
  assign controlled_buffer_1_out = comparevalue_1_comcri ? comparevalue_1_cri_2 : 8'bz;  // Controlled_Buffer controlled_buffer_25
  or or_23 (or_23_out, or_15_out, comparevalue_1_comcle);
  assign controlled_buffer_6_out = comparevalue_1_comcle ? comparevalue_1_cle : 12'bz;  // Controlled_Buffer controlled_buffer_26
  or or_24 (or_24_out, or_19_out, comparevalue_1_comcli);
  assign controlled_buffer_2_out = comparevalue_1_comcli ? comparevalue_1_cli_2 : 8'bz;  // Controlled_Buffer controlled_buffer_27
  or or_25 (or_25_out, or_20_out, immediateresolution_1_immpib);
  assign controlled_buffer_20_out = immediateresolution_1_immpib ? immediateresolution_1_out_3 : 8'bz;  // Controlled_Buffer controlled_buffer_28
  ImmediateResolution immediateresolution_1 (
    .ActivationSignal(decoder_1_out7), .ImmPIB(immediateresolution_1_immpib),
    .out_3(immediateresolution_1_out_3));
  PrepareForTransformationAsAncestorInput preparefortransformationasancestorinput_1 (
    .ActivationSignal(decoder_1_out8), .Clock(Clock), .SFS(SFS), .SBS(SBS), .RAM(RAM),
    .UniqueNodeID(UniqueNodeID), .CLI(CLI), .CRI(CRI), .CLE(CLE), .CRE(CRE),
    .InternalExpression(InternalExpression), .ptaRAM(preparefortransformationasancestorinput_1_ptaram),
    .ptaSFS(preparefortransformationasancestorinput_1_ptasfs),
    .ptaPEB(preparefortransformationasancestorinput_1_ptapeb),
    .ptaCLI(preparefortransformationasancestorinput_1_ptacli),
    .ptaCRI(preparefortransformationasancestorinput_1_ptacri),
    .ptaSEL(preparefortransformationasancestorinput_1_ptasel),
    .ptaSBS(preparefortransformationasancestorinput_1_ptasbs),
    .ptaStackClear(preparefortransformationasancestorinput_1_ptastackclear),
    .ptaPIB(preparefortransformationasancestorinput_1_ptapib),
    .GeneralOuput(preparefortransformationasancestorinput_1_generalouput),
    .PEB(preparefortransformationasancestorinput_1_peb),
    .CLI_2(preparefortransformationasancestorinput_1_cli_2),
    .CRI_2(preparefortransformationasancestorinput_1_cri_2),
    .PIB(preparefortransformationasancestorinput_1_pib));
  or or_26 (or_26_out, returnexpression_1_retpeb, preparefortransformationasancestorinput_1_ptapeb);
  assign controlled_buffer_19_out = preparefortransformationasancestorinput_1_ptapeb ? preparefortransformationasancestorinput_1_peb : 12'bz;  // Controlled_Buffer controlled_buffer_29
  or or_27 (or_27_out, or_25_out, preparefortransformationasancestorinput_1_ptapib);
  assign controlled_buffer_20_out = preparefortransformationasancestorinput_1_ptapib ? preparefortransformationasancestorinput_1_pib : 8'bz;  // Controlled_Buffer controlled_buffer_30
  or or_28 (or_28_out, or_22_out, preparefortransformationasancestorinput_1_ptacri);
  assign controlled_buffer_1_out = preparefortransformationasancestorinput_1_ptacri ? preparefortransformationasancestorinput_1_cri_2 : 8'bz;  // Controlled_Buffer controlled_buffer_31
  or or_29 (or_29_out, or_24_out, preparefortransformationasancestorinput_1_ptacli);
  assign controlled_buffer_2_out = preparefortransformationasancestorinput_1_ptacli ? preparefortransformationasancestorinput_1_cli_2 : 8'bz;  // Controlled_Buffer controlled_buffer_32
  or or_30 (or_30_out, or_5_out, preparefortransformationasancestorinput_1_ptastackclear);
  or or_31 (or_31_out, preparefortransformationasancestorinput_1_ptaram, preparefortransformationasancestorinput_1_ptasfs, preparefortransformationasancestorinput_1_ptasbs);
  assign controlled_buffer_33_out = or_31_out ? preparefortransformationasancestorinput_1_generalouput : 8'bz;  // Controlled_Buffer controlled_buffer_33
  or or_32 (or_32_out, preparefortransformationasancestorinput_1_ptasel, preparefortransformationasdecendantinput_1_ptdsel);
  or or_33 (or_33_out, preparefortransformationasancestorinput_1_ptasbs, preparefortransformationasdecendantinput_1_ptdsbs);
  or or_34 (or_34_out, preparefortransformationasancestorinput_1_ptasfs, preparefortransformationasdecendantinput_1_ptdsfs);
  or or_35 (or_35_out, preparefortransformationasancestorinput_1_ptaram, preparefortransformationasdecendantinput_1_ptdram);
  or or_36 (or_36_out, or_12_out, preparefortransformationasdecendantinput_1_ptdexp);
  PrepareForTransformationAsDecendantInput preparefortransformationasdecendantinput_1 (
    .ActivationSignal(decoder_1_out9), .Clock(Clock), .TransformMark(comparevalue_1_markfortransformation),
    .InExp(InternalExpression), .SFS(SFS), .SBS(SBS), .UniqueNodeID(UniqueNodeID), .RAM(RAM),
    .NewNodeID(NewNodeID), .PIB(PIB), .Buffer(Buffer), .PEB(PEB), .CLI(CLI), .CRI(CRI),
    .ptdCLC(preparefortransformationasdecendantinput_1_ptdclc),
    .ptdRAM(preparefortransformationasdecendantinput_1_ptdram),
    .ptdSFS(preparefortransformationasdecendantinput_1_ptdsfs), .PtdToggleChildren(NameToggleChildren),
    .ptdSEL(preparefortransformationasdecendantinput_1_ptdsel),
    .ptdNEW(preparefortransformationasdecendantinput_1_ptdnew), .PtdBUF(BufferWrite),
    .ptdCRI(preparefortransformationasdecendantinput_1_ptdcri),
    .ptdCLI(preparefortransformationasdecendantinput_1_ptdcli),
    .ptdCRE(preparefortransformationasdecendantinput_1_ptdcre),
    .ptdCLE(preparefortransformationasdecendantinput_1_ptdcle),
    .PtdEXP(preparefortransformationasdecendantinput_1_ptdexp),
    .ptdSBS(preparefortransformationasdecendantinput_1_ptdsbs),
    .ptdPIB(preparefortransformationasdecendantinput_1_ptdpib),
    .ptdStackclear(preparefortransformationasdecendantinput_1_ptdstackclear),
    .ptdCompareValueClear(preparefortransformationasdecendantinput_1_ptdcomparevalueclear),
    .Output(preparefortransformationasdecendantinput_1_output),
    .CLI_2(preparefortransformationasdecendantinput_1_cli_2),
    .CLE(preparefortransformationasdecendantinput_1_cle),
    .CRI_2(preparefortransformationasdecendantinput_1_cri_2),
    .CRE(preparefortransformationasdecendantinput_1_cre),
    .PIB_2(preparefortransformationasdecendantinput_1_pib_2),
    .NewExpression(preparefortransformationasdecendantinput_1_newexpression));
  assign RamSelect = and_1_out ? or_32_out : 1'bz;  // Controlled_Buffer controlled_buffer_34
  assign BackStack = and_1_out ? or_33_out : 1'bz;  // Controlled_Buffer controlled_buffer_35
  assign FrontStack = and_1_out ? or_34_out : 1'bz;  // Controlled_Buffer controlled_buffer_36
  assign RAMwrite = and_1_out ? or_35_out : 1'bz;  // Controlled_Buffer controlled_buffer_37
  assign EXPWrite = and_1_out ? or_36_out : 1'bz;  // Controlled_Buffer controlled_buffer_38
  assign NewNode = and_1_out ? preparefortransformationasdecendantinput_1_ptdnew : 1'bz;  // Controlled_Buffer controlled_buffer_39
  or or_37 (or_37_out, or_27_out, preparefortransformationasdecendantinput_1_ptdpib);
  assign controlled_buffer_20_out = preparefortransformationasdecendantinput_1_ptdpib ? preparefortransformationasdecendantinput_1_pib_2 : 8'bz;  // Controlled_Buffer controlled_buffer_40
  or or_38 (or_38_out, or_21_out, preparefortransformationasdecendantinput_1_ptdcre);
  assign controlled_buffer_4_out = preparefortransformationasdecendantinput_1_ptdcre ? preparefortransformationasdecendantinput_1_cre : 12'bz;  // Controlled_Buffer controlled_buffer_41
  or or_39 (or_39_out, or_28_out, preparefortransformationasdecendantinput_1_ptdcri);
  assign controlled_buffer_1_out = preparefortransformationasdecendantinput_1_ptdcri ? preparefortransformationasdecendantinput_1_cri_2 : 8'bz;  // Controlled_Buffer controlled_buffer_42
  or or_40 (or_40_out, or_23_out, preparefortransformationasdecendantinput_1_ptdcle);
  assign controlled_buffer_6_out = preparefortransformationasdecendantinput_1_ptdcle ? preparefortransformationasdecendantinput_1_cle : 12'bz;  // Controlled_Buffer controlled_buffer_43
  or or_41 (or_41_out, or_29_out, preparefortransformationasdecendantinput_1_ptdcli);
  assign controlled_buffer_2_out = preparefortransformationasdecendantinput_1_ptdcli ? preparefortransformationasdecendantinput_1_cli_2 : 8'bz;  // Controlled_Buffer controlled_buffer_44
  or or_42 (or_42_out, or_17_out, preparefortransformationasdecendantinput_1_ptdexp);
  assign controlled_buffer_3_out = preparefortransformationasdecendantinput_1_ptdexp ? preparefortransformationasdecendantinput_1_newexpression : 12'bz;  // Controlled_Buffer controlled_buffer_45
  or or_43 (or_43_out, or_30_out, preparefortransformationasdecendantinput_1_ptdstackclear);
  or or_44 (or_44_out, preparefortransformationasdecendantinput_1_ptdram, preparefortransformationasdecendantinput_1_ptdsfs, preparefortransformationasdecendantinput_1_ptdsbs, BufferWrite);
  not not_2 (not_2_out, or_26_out);
  not not_3 (not_3_out, or_37_out);
  not not_4 (not_4_out, or_38_out);
  not not_5 (not_5_out, or_39_out);
  not not_6 (not_6_out, or_40_out);
  not not_7 (not_7_out, or_41_out);
  not not_8 (not_8_out, or_42_out);
  or or_45 (or_45_out, or_31_out, or_44_out);
  assign controlled_buffer_33_out = or_44_out ? preparefortransformationasdecendantinput_1_output : 8'bz;  // Controlled_Buffer controlled_buffer_46
  assign controlled_buffer_19_out = not_2_out ? InternalExpression : 12'bz;  // Controlled_Buffer controlled_buffer_47
  assign controlled_buffer_20_out = not_3_out ? {8{1'b0}} : 8'bz;  // Controlled_Buffer controlled_buffer_48
  assign controlled_buffer_4_out = not_4_out ? {12{1'b0}} : 12'bz;  // Controlled_Buffer controlled_buffer_49
  assign controlled_buffer_1_out = not_5_out ? {8{1'b0}} : 8'bz;  // Controlled_Buffer controlled_buffer_50
  assign controlled_buffer_6_out = not_6_out ? {12{1'b0}} : 12'bz;  // Controlled_Buffer controlled_buffer_51
  assign controlled_buffer_2_out = not_7_out ? {8{1'b0}} : 8'bz;  // Controlled_Buffer controlled_buffer_52
  assign controlled_buffer_3_out = not_8_out ? {12{1'b0}} : 12'bz;  // Controlled_Buffer controlled_buffer_53
  not not_9 (not_9_out, or_45_out);
  assign controlled_buffer_33_out = not_9_out ? {8{1'b0}} : 8'bz;  // Controlled_Buffer controlled_buffer_54
  assign ClearChidlren = and_1_out ? preparefortransformationasdecendantinput_1_ptdclc : 1'bz;  // Controlled_Buffer controlled_buffer_55
  assign PEB_2 = and_1_out ? controlled_buffer_19_out : 12'bz;  // Controlled_Buffer controlled_buffer_56
  assign PIB_2 = and_1_out ? controlled_buffer_20_out : 8'bz;  // Controlled_Buffer controlled_buffer_57
  assign CRE_2 = and_1_out ? controlled_buffer_4_out : 12'bz;  // Controlled_Buffer controlled_buffer_58
  assign CRI_2 = and_1_out ? controlled_buffer_1_out : 8'bz;  // Controlled_Buffer controlled_buffer_59
  assign CLE_2 = and_1_out ? controlled_buffer_6_out : 12'bz;  // Controlled_Buffer controlled_buffer_60
  assign CLI_2 = and_1_out ? controlled_buffer_2_out : 8'bz;  // Controlled_Buffer controlled_buffer_61
  assign NewNode_2 = and_1_out ? controlled_buffer_3_out : 12'bz;  // Controlled_Buffer controlled_buffer_62
  assign GeneralOutput = and_1_out ? controlled_buffer_33_out : 8'bz;  // Controlled_Buffer controlled_buffer_63
  assign StackClear = and_1_out ? or_43_out : 1'bz;  // Controlled_Buffer controlled_buffer_64

  // Notes on the sheet:
  //   Input
  //   0 == Backstack / 1 == Frontstack
  //   Output
endmodule

module GoToExpression (
  input  [11:0] PEB,
  input  [7:0] PIB,
  input  [11:0] CRE,
  input  [7:0] CRI,
  input  [11:0] CLE,
  input  [7:0] CLI,
  input  [3:0] SFS,
  input  [3:0] SBS,
  input  [3:0] RAM,
  input  [11:0] InternalExpression,
  input  [2:0] Buffer,
  input  Clock,
  input  [3:0] NewNodeID,
  input  [3:0] UniqueNodeID,
  output EXPWrite,
  output RamSelect,
  output FrontStack,
  output BackStack,
  output RAMwrite,
  output NewNode,
  output [11:0] PEB_2,
  output [7:0] PIB_2,
  output [11:0] CRE_2,
  output [7:0] CRI_2,
  output [11:0] CLE_2,
  output [7:0] CLI_2,
  output [11:0] NewNode_2,
  output [7:0] GeneralOutput,
  output ClearChidlren,
  output StackClear
);

  wire and_1_out, decoder_1_out1, decoder_1_out2, decoder_1_out3, decoder_1_out4, decoder_1_out5, not_2_out,
       not_3_out, not_4_out, not_5_out, not_6_out, not_7_out, not_8_out, nullification_1_nullcli,
       nullification_1_nullcri, nullification_1_nullexp, nullification_1_nullstackclear, or_1_out, or_2_out,
       or_3_out, or_4_out, or_5_out, or_6_out, or_7_out, or_8_out, or_9_out, or_10_out, or_11_out, or_12_out,
       or_13_out, or_14_out, or_15_out, or_16_out, or_17_out, or_18_out, or_19_out,
       returnexpression_1_retcli, returnexpression_1_retcri, returnexpression_1_retpeb,
       returnexpression_1_retpib, updateexpression_1_updcle, updateexpression_1_updcli,
       updateexpression_1_updcre, updateexpression_1_updcri, updateexpression_1_updexp,
       updateexpression_1_updstackclear, updatepointerleft_1_updcle, updatepointerleft_1_updcli,
       updatepointerleft_1_updcre, updatepointerleft_1_updcri, updatepointerleft_1_updexp,
       updatepointerright_1_updcle, updatepointerright_1_updcli, updatepointerright_1_updcre,
       updatepointerright_1_updcri, updatepointerright_1_updexp;
  wire [2:0] not_1_out, xor_1_out;
  wire [7:0] controlled_buffer_1_out, controlled_buffer_2_out, controlled_buffer_20_out, nullification_1_cli,
       nullification_1_cri, returnexpression_1_cli_2, returnexpression_1_cri_2, returnexpression_1_pib_2,
       updateexpression_1_cli, updateexpression_1_cri, updatepointerleft_1_cli, updatepointerleft_1_cri,
       updatepointerright_1_cli, updatepointerright_1_cri;
  wire [11:0] controlled_buffer_3_out, controlled_buffer_4_out, controlled_buffer_6_out,
       controlled_buffer_19_out, nullification_1_newvalue, returnexpression_1_peb, updateexpression_1_cle,
       updateexpression_1_cre, updateexpression_1_newvalue, updatepointerleft_1_cle, updatepointerleft_1_cre,
       updatepointerleft_1_newvalue, updatepointerright_1_cli_2, updatepointerright_1_cri_2,
       updatepointerright_1_newvalue;

  Decoder #(.select(4)) decoder_1 (
    .out1(decoder_1_out1), .out2(decoder_1_out2), .out3(decoder_1_out3), .out4(decoder_1_out4),
    .out5(decoder_1_out5), .sel(PIB[7:4]));  // open: out0, out6, out7, out8, out9, out10, out11, out12, out13, out14, out15, en
  Nullification nullification_1 (
    .ActivationSignal(decoder_1_out1), .Clock(Clock), .NullCLI(nullification_1_nullcli),
    .NullCRI(nullification_1_nullcri), .NullStackClear(nullification_1_nullstackclear),
    .NullEXP(nullification_1_nullexp), .CRI(nullification_1_cri), .CLI(nullification_1_cli),
    .NewValue(nullification_1_newvalue));
  assign controlled_buffer_1_out = nullification_1_nullcli ? nullification_1_cri : 8'bz;  // Controlled_Buffer controlled_buffer_1
  assign controlled_buffer_2_out = nullification_1_nullcri ? nullification_1_cli : 8'bz;  // Controlled_Buffer controlled_buffer_2
  assign controlled_buffer_3_out = nullification_1_nullexp ? nullification_1_newvalue : 12'bz;  // Controlled_Buffer controlled_buffer_3
  UpdateExpression updateexpression_1 (
    .ActivationSignal(decoder_1_out2), .Clock(Clock), .UniqueNodeID(UniqueNodeID), .PIB(PIB), .PEB(PEB),
    .UpdCLE(updateexpression_1_updcle), .UpdCRE(updateexpression_1_updcre),
    .UpdCLI(updateexpression_1_updcli), .UpdCRI(updateexpression_1_updcri),
    .UpdStackClear(updateexpression_1_updstackclear), .UpdEXP(updateexpression_1_updexp),
    .CRI(updateexpression_1_cri), .CLI(updateexpression_1_cli), .CRE(updateexpression_1_cre),
    .CLE(updateexpression_1_cle), .NewValue(updateexpression_1_newvalue));
  assign not_1_out = ~xor_1_out;  // NOT_Gate not_1, 3 bits wide
  assign xor_1_out = InternalExpression[10:8] ^ 3'b100;  // XOR_Gate xor_1, 3 bits wide
  or or_1 (or_1_out, nullification_1_nullexp, updateexpression_1_updexp);
  assign controlled_buffer_4_out = updateexpression_1_updcre ? updateexpression_1_cre : 12'bz;  // Controlled_Buffer controlled_buffer_4
  or or_2 (or_2_out, nullification_1_nullcli, updateexpression_1_updcri);
  assign controlled_buffer_1_out = updateexpression_1_updcri ? updateexpression_1_cri : 8'bz;  // Controlled_Buffer controlled_buffer_5
  assign controlled_buffer_6_out = updateexpression_1_updcle ? updateexpression_1_cle : 12'bz;  // Controlled_Buffer controlled_buffer_6
  or or_3 (or_3_out, nullification_1_nullcri, updateexpression_1_updcli);
  assign controlled_buffer_2_out = updateexpression_1_updcli ? updateexpression_1_cli : 8'bz;  // Controlled_Buffer controlled_buffer_7
  or or_4 (or_4_out, nullification_1_nullexp, updateexpression_1_updexp);
  assign controlled_buffer_3_out = updateexpression_1_updexp ? updateexpression_1_newvalue : 12'bz;  // Controlled_Buffer controlled_buffer_8
  or or_5 (or_5_out, nullification_1_nullstackclear, updateexpression_1_updstackclear);
  and and_1 (and_1_out, not_1_out[0], not_1_out[1], not_1_out[2]);
  UpdatePointerLeft updatepointerleft_1 (
    .ActivationSignal(decoder_1_out3), .Clock(Clock), .UniqueNodeID(UniqueNodeID), .PIB(PIB),
    .InternalExpression(InternalExpression), .PEB(PEB), .UpdCLE(updatepointerleft_1_updcle),
    .UpdCRE(updatepointerleft_1_updcre), .UpdCLI(updatepointerleft_1_updcli),
    .UpdCRI(updatepointerleft_1_updcri), .UpdEXP(updatepointerleft_1_updexp), .CRI(updatepointerleft_1_cri),
    .CLI(updatepointerleft_1_cli), .CRE(updatepointerleft_1_cre), .CLE(updatepointerleft_1_cle),
    .NewValue(updatepointerleft_1_newvalue));
  or or_6 (or_6_out, or_1_out, updatepointerleft_1_updexp);
  or or_7 (or_7_out, updateexpression_1_updcre, updatepointerleft_1_updcre);
  assign controlled_buffer_4_out = updatepointerleft_1_updcre ? updatepointerleft_1_cre : 12'bz;  // Controlled_Buffer controlled_buffer_9
  or or_8 (or_8_out, or_2_out, updatepointerleft_1_updcri);
  assign controlled_buffer_1_out = updatepointerleft_1_updcri ? updatepointerleft_1_cri : 8'bz;  // Controlled_Buffer controlled_buffer_10
  or or_9 (or_9_out, updateexpression_1_updcle, updatepointerleft_1_updcle);
  assign controlled_buffer_6_out = updatepointerleft_1_updcle ? updatepointerleft_1_cle : 12'bz;  // Controlled_Buffer controlled_buffer_11
  or or_10 (or_10_out, or_3_out, updatepointerleft_1_updcli);
  assign controlled_buffer_2_out = updatepointerleft_1_updcli ? updatepointerleft_1_cli : 8'bz;  // Controlled_Buffer controlled_buffer_12
  or or_11 (or_11_out, or_4_out, updatepointerleft_1_updexp);
  assign controlled_buffer_3_out = updatepointerleft_1_updexp ? updatepointerleft_1_newvalue : 12'bz;  // Controlled_Buffer controlled_buffer_13
  UpdatePointerRight updatepointerright_1 (
    .ActivationSignal(decoder_1_out4), .Clock(Clock), .UniqueNodeID(UniqueNodeID), .PIB(PIB),
    .InternalExpression(InternalExpression), .PEB(PEB), .UpdCLE(updatepointerright_1_updcle),
    .UpdCRE(updatepointerright_1_updcre), .UpdCLI(updatepointerright_1_updcli),
    .UpdCRI(updatepointerright_1_updcri), .UpdEXP(updatepointerright_1_updexp),
    .CRI(updatepointerright_1_cri), .CLI(updatepointerright_1_cli), .CRI_2(updatepointerright_1_cri_2),
    .CLI_2(updatepointerright_1_cli_2), .NewValue(updatepointerright_1_newvalue));
  or or_12 (or_12_out, or_6_out, updatepointerright_1_updexp);
  or or_13 (or_13_out, or_7_out, updatepointerright_1_updcre);
  assign controlled_buffer_4_out = updatepointerright_1_updcre ? updatepointerright_1_cri_2 : 12'bz;  // Controlled_Buffer controlled_buffer_14
  or or_14 (or_14_out, or_8_out, updatepointerright_1_updcri);
  assign controlled_buffer_1_out = updatepointerright_1_updcri ? updatepointerright_1_cri : 8'bz;  // Controlled_Buffer controlled_buffer_15
  or or_15 (or_15_out, or_9_out, updatepointerright_1_updcle);
  assign controlled_buffer_6_out = updatepointerright_1_updcle ? updatepointerright_1_cli_2 : 12'bz;  // Controlled_Buffer controlled_buffer_16
  or or_16 (or_16_out, or_10_out, updatepointerright_1_updcli);
  assign controlled_buffer_2_out = updatepointerright_1_updcli ? updatepointerright_1_cli : 8'bz;  // Controlled_Buffer controlled_buffer_17
  or or_17 (or_17_out, or_11_out, updatepointerright_1_updexp);
  assign controlled_buffer_3_out = updatepointerright_1_updexp ? updatepointerright_1_newvalue : 12'bz;  // Controlled_Buffer controlled_buffer_18
  assign controlled_buffer_19_out = returnexpression_1_retpeb ? returnexpression_1_peb : 12'bz;  // Controlled_Buffer controlled_buffer_19
  assign controlled_buffer_20_out = returnexpression_1_retpib ? returnexpression_1_pib_2 : 8'bz;  // Controlled_Buffer controlled_buffer_20
  or or_18 (or_18_out, or_14_out, returnexpression_1_retcri);
  assign controlled_buffer_1_out = returnexpression_1_retcri ? returnexpression_1_cri_2 : 8'bz;  // Controlled_Buffer controlled_buffer_21
  ReturnExpression returnexpression_1 (
    .ActivationSignal(decoder_1_out5), .UniqueNodeID(UniqueNodeID), .PIB(PIB), .CLI(CLI), .CRI(CRI),
    .CRE(CRE), .CLE(CLE), .InternalExpression(InternalExpression), .RetCLI(returnexpression_1_retcli),
    .RetCRI(returnexpression_1_retcri), .RetPIB(returnexpression_1_retpib),
    .RetPEB(returnexpression_1_retpeb), .CRI_2(returnexpression_1_cri_2), .CLI_2(returnexpression_1_cli_2),
    .PEB(returnexpression_1_peb), .PIB_2(returnexpression_1_pib_2));
  assign RamSelect = and_1_out ? 1'b0 : 1'bz;  // Controlled_Buffer controlled_buffer_22
  assign BackStack = and_1_out ? 1'b0 : 1'bz;  // Controlled_Buffer controlled_buffer_23
  assign FrontStack = and_1_out ? 1'b0 : 1'bz;  // Controlled_Buffer controlled_buffer_24
  assign RAMwrite = and_1_out ? 1'b0 : 1'bz;  // Controlled_Buffer controlled_buffer_25
  assign EXPWrite = and_1_out ? or_12_out : 1'bz;  // Controlled_Buffer controlled_buffer_26
  assign NewNode = and_1_out ? 1'b0 : 1'bz;  // Controlled_Buffer controlled_buffer_27
  or or_19 (or_19_out, or_16_out, returnexpression_1_retcli);
  assign controlled_buffer_2_out = returnexpression_1_retcli ? returnexpression_1_cli_2 : 8'bz;  // Controlled_Buffer controlled_buffer_28
  not not_2 (not_2_out, returnexpression_1_retpeb);
  assign controlled_buffer_19_out = not_2_out ? CRE : 12'bz;  // Controlled_Buffer controlled_buffer_29
  not not_3 (not_3_out, returnexpression_1_retpib);
  assign controlled_buffer_20_out = not_3_out ? CRI : 8'bz;  // Controlled_Buffer controlled_buffer_30
  not not_4 (not_4_out, or_13_out);
  assign controlled_buffer_4_out = not_4_out ? PEB : 12'bz;  // Controlled_Buffer controlled_buffer_31
  not not_5 (not_5_out, or_18_out);
  assign controlled_buffer_1_out = not_5_out ? PIB : 8'bz;  // Controlled_Buffer controlled_buffer_32
  not not_6 (not_6_out, or_15_out);
  assign controlled_buffer_6_out = not_6_out ? {12{1'b0}} : 12'bz;  // Controlled_Buffer controlled_buffer_33
  not not_7 (not_7_out, or_19_out);
  assign controlled_buffer_2_out = not_7_out ? {8{1'b0}} : 8'bz;  // Controlled_Buffer controlled_buffer_34
  not not_8 (not_8_out, or_17_out);
  assign controlled_buffer_3_out = not_8_out ? {12{1'b0}} : 12'bz;  // Controlled_Buffer controlled_buffer_35
  assign ClearChidlren = and_1_out ? 1'b0 : 1'bz;  // Controlled_Buffer controlled_buffer_36
  assign StackClear = and_1_out ? or_5_out : 1'bz;  // Controlled_Buffer controlled_buffer_37
  assign PEB_2 = and_1_out ? controlled_buffer_19_out : 12'bz;  // Controlled_Buffer controlled_buffer_38
  assign PIB_2 = and_1_out ? controlled_buffer_20_out : 8'bz;  // Controlled_Buffer controlled_buffer_39
  assign CRE_2 = and_1_out ? controlled_buffer_4_out : 12'bz;  // Controlled_Buffer controlled_buffer_40
  assign CRI_2 = and_1_out ? controlled_buffer_1_out : 8'bz;  // Controlled_Buffer controlled_buffer_41
  assign CLE_2 = and_1_out ? controlled_buffer_6_out : 12'bz;  // Controlled_Buffer controlled_buffer_42
  assign CLI_2 = and_1_out ? controlled_buffer_2_out : 8'bz;  // Controlled_Buffer controlled_buffer_43
  assign NewNode_2 = and_1_out ? controlled_buffer_3_out : 12'bz;  // Controlled_Buffer controlled_buffer_44
  assign GeneralOutput = and_1_out ? {8{1'b0}} : 8'bz;  // Controlled_Buffer controlled_buffer_45

  // Notes on the sheet:
  //   Input
  //   0 == Backstack / 1 == Frontstack
  //   Output
endmodule

module ApplicationExpression (
  input  [11:0] PEB,
  input  [7:0] PIB,
  input  [11:0] CRE,
  input  [7:0] CRI,
  input  [11:0] CLE,
  input  [7:0] CLI,
  input  [3:0] SFS,
  input  [3:0] SBS,
  input  [3:0] RAM,
  input  [11:0] InternalExpression,
  input  [2:0] Buffer,
  input  Clock,
  input  [3:0] NewNodeID,
  input  [3:0] UniqueNodeID,
  output EXPWrite,
  output RamSelect,
  output FrontStack,
  output BackStack,
  output RAMwrite,
  output NewNode,
  output [11:0] PEB_2,
  output [7:0] PIB_2,
  output [11:0] CRE_2,
  output [7:0] CRI_2,
  output [11:0] CLE_2,
  output [7:0] CLI_2,
  output [11:0] NewNode_2,
  output [7:0] GeneralOutput,
  output ClearChidlren,
  output StackClear
);

  wire and_1_out, branchchop_1_branew, comparevalue_1_comcle, comparevalue_1_comcli, comparevalue_1_comcre,
       comparevalue_1_comcri, comparevalue_1_compib, comparevalue_1_markfortransformation, decoder_1_out1,
       decoder_1_out2, decoder_1_out3, decoder_1_out4, decoder_1_out5, decoder_1_out6, decoder_1_out9,
       not_2_out, not_3_out, not_4_out, not_5_out, not_6_out, not_7_out, not_8_out, not_9_out,
       nullification_1_nullcli, nullification_1_nullcri, nullification_1_nullexp,
       nullification_1_nullstackclear, or_1_out, or_2_out, or_3_out, or_4_out, or_5_out, or_6_out, or_7_out,
       or_8_out, or_9_out, or_10_out, or_11_out, or_12_out, or_13_out, or_14_out, or_15_out, or_16_out,
       or_17_out, or_18_out, or_19_out, or_20_out, or_21_out, or_22_out, or_23_out, or_24_out, or_25_out,
       or_26_out, or_27_out, or_28_out, or_29_out, or_30_out, or_31_out, or_32_out, or_33_out, or_34_out,
       preparefortransformationasdecendantinput_1_ptdbuf, preparefortransformationasdecendantinput_1_ptdclc,
       preparefortransformationasdecendantinput_1_ptdcle, preparefortransformationasdecendantinput_1_ptdcli,
       preparefortransformationasdecendantinput_1_ptdcomparevalueclear,
       preparefortransformationasdecendantinput_1_ptdcre, preparefortransformationasdecendantinput_1_ptdcri,
       preparefortransformationasdecendantinput_1_ptdexp, preparefortransformationasdecendantinput_1_ptdnew,
       preparefortransformationasdecendantinput_1_ptdpib, preparefortransformationasdecendantinput_1_ptdram,
       preparefortransformationasdecendantinput_1_ptdsbs, preparefortransformationasdecendantinput_1_ptdsel,
       preparefortransformationasdecendantinput_1_ptdsfs,
       preparefortransformationasdecendantinput_1_ptdstackclear, returnexpression_1_retcli,
       returnexpression_1_retcri, returnexpression_1_retpeb, returnexpression_1_retpib,
       updateexpression_1_updcle, updateexpression_1_updcli, updateexpression_1_updcre,
       updateexpression_1_updcri, updateexpression_1_updexp, updateexpression_1_updstackclear,
       updatepointerleft_1_updcle, updatepointerleft_1_updcli, updatepointerleft_1_updcre,
       updatepointerleft_1_updcri, updatepointerleft_1_updexp, updatepointerright_1_updcle,
       updatepointerright_1_updcli, updatepointerright_1_updcre, updatepointerright_1_updcri,
       updatepointerright_1_updexp;
  wire [2:0] not_1_out, xor_1_out;
  wire [7:0] comparevalue_1_cli_2, comparevalue_1_cri_2, comparevalue_1_pib_2, controlled_buffer_1_out,
       controlled_buffer_2_out, controlled_buffer_20_out, controlled_buffer_40_out, nullification_1_cli,
       nullification_1_cri, preparefortransformationasdecendantinput_1_cli_2,
       preparefortransformationasdecendantinput_1_cri_2, preparefortransformationasdecendantinput_1_output,
       preparefortransformationasdecendantinput_1_pib_2, returnexpression_1_cli_2, returnexpression_1_cri_2,
       returnexpression_1_pib_2, updateexpression_1_cli, updateexpression_1_cri, updatepointerleft_1_cli,
       updatepointerleft_1_cri, updatepointerright_1_cli, updatepointerright_1_cri;
  wire [11:0] branchchop_1_newvalue, comparevalue_1_cle, comparevalue_1_cre, controlled_buffer_3_out,
       controlled_buffer_4_out, controlled_buffer_6_out, controlled_buffer_19_out, nullification_1_newvalue,
       preparefortransformationasdecendantinput_1_cle, preparefortransformationasdecendantinput_1_cre,
       preparefortransformationasdecendantinput_1_newexpression, returnexpression_1_peb,
       updateexpression_1_cle, updateexpression_1_cre, updateexpression_1_newvalue, updatepointerleft_1_cle,
       updatepointerleft_1_cre, updatepointerleft_1_newvalue, updatepointerright_1_cli_2,
       updatepointerright_1_cri_2, updatepointerright_1_newvalue;

  Decoder #(.select(4)) decoder_1 (
    .out1(decoder_1_out1), .out2(decoder_1_out2), .out3(decoder_1_out3), .out4(decoder_1_out4),
    .out5(decoder_1_out5), .out6(decoder_1_out6), .out9(decoder_1_out9), .sel(PIB[7:4]));  // open: out0, out7, out8, out10, out11, out12, out13, out14, out15, en
  Nullification nullification_1 (
    .ActivationSignal(decoder_1_out1), .Clock(Clock), .NullCLI(nullification_1_nullcli),
    .NullCRI(nullification_1_nullcri), .NullStackClear(nullification_1_nullstackclear),
    .NullEXP(nullification_1_nullexp), .CRI(nullification_1_cri), .CLI(nullification_1_cli),
    .NewValue(nullification_1_newvalue));
  assign controlled_buffer_1_out = nullification_1_nullcli ? nullification_1_cri : 8'bz;  // Controlled_Buffer controlled_buffer_1
  assign controlled_buffer_2_out = nullification_1_nullcri ? nullification_1_cli : 8'bz;  // Controlled_Buffer controlled_buffer_2
  assign controlled_buffer_3_out = nullification_1_nullexp ? nullification_1_newvalue : 12'bz;  // Controlled_Buffer controlled_buffer_3
  UpdateExpression updateexpression_1 (
    .ActivationSignal(decoder_1_out2), .Clock(Clock), .UniqueNodeID(UniqueNodeID), .PIB(PIB), .PEB(PEB),
    .UpdCLE(updateexpression_1_updcle), .UpdCRE(updateexpression_1_updcre),
    .UpdCLI(updateexpression_1_updcli), .UpdCRI(updateexpression_1_updcri),
    .UpdStackClear(updateexpression_1_updstackclear), .UpdEXP(updateexpression_1_updexp),
    .CRI(updateexpression_1_cri), .CLI(updateexpression_1_cli), .CRE(updateexpression_1_cre),
    .CLE(updateexpression_1_cle), .NewValue(updateexpression_1_newvalue));
  assign not_1_out = ~xor_1_out;  // NOT_Gate not_1, 3 bits wide
  assign xor_1_out = InternalExpression[10:8] ^ 3'b010;  // XOR_Gate xor_1, 3 bits wide
  or or_1 (or_1_out, nullification_1_nullexp, updateexpression_1_updexp);
  assign controlled_buffer_4_out = updateexpression_1_updcre ? updateexpression_1_cre : 12'bz;  // Controlled_Buffer controlled_buffer_4
  or or_2 (or_2_out, nullification_1_nullcli, updateexpression_1_updcri);
  assign controlled_buffer_1_out = updateexpression_1_updcri ? updateexpression_1_cri : 8'bz;  // Controlled_Buffer controlled_buffer_5
  assign controlled_buffer_6_out = updateexpression_1_updcle ? updateexpression_1_cle : 12'bz;  // Controlled_Buffer controlled_buffer_6
  or or_3 (or_3_out, nullification_1_nullcri, updateexpression_1_updcli);
  assign controlled_buffer_2_out = updateexpression_1_updcli ? updateexpression_1_cli : 8'bz;  // Controlled_Buffer controlled_buffer_7
  or or_4 (or_4_out, nullification_1_nullexp, updateexpression_1_updexp);
  assign controlled_buffer_3_out = updateexpression_1_updexp ? updateexpression_1_newvalue : 12'bz;  // Controlled_Buffer controlled_buffer_8
  or or_5 (or_5_out, nullification_1_nullstackclear, updateexpression_1_updstackclear);
  and and_1 (and_1_out, not_1_out[0], not_1_out[1], not_1_out[2]);
  UpdatePointerLeft updatepointerleft_1 (
    .ActivationSignal(decoder_1_out3), .Clock(Clock), .UniqueNodeID(UniqueNodeID), .PIB(PIB),
    .InternalExpression(InternalExpression), .PEB(PEB), .UpdCLE(updatepointerleft_1_updcle),
    .UpdCRE(updatepointerleft_1_updcre), .UpdCLI(updatepointerleft_1_updcli),
    .UpdCRI(updatepointerleft_1_updcri), .UpdEXP(updatepointerleft_1_updexp), .CRI(updatepointerleft_1_cri),
    .CLI(updatepointerleft_1_cli), .CRE(updatepointerleft_1_cre), .CLE(updatepointerleft_1_cle),
    .NewValue(updatepointerleft_1_newvalue));
  or or_6 (or_6_out, or_1_out, updatepointerleft_1_updexp);
  or or_7 (or_7_out, updateexpression_1_updcre, updatepointerleft_1_updcre);
  assign controlled_buffer_4_out = updatepointerleft_1_updcre ? updatepointerleft_1_cre : 12'bz;  // Controlled_Buffer controlled_buffer_9
  or or_8 (or_8_out, or_2_out, updatepointerleft_1_updcri);
  assign controlled_buffer_1_out = updatepointerleft_1_updcri ? updatepointerleft_1_cri : 8'bz;  // Controlled_Buffer controlled_buffer_10
  or or_9 (or_9_out, updateexpression_1_updcle, updatepointerleft_1_updcle);
  assign controlled_buffer_6_out = updatepointerleft_1_updcle ? updatepointerleft_1_cle : 12'bz;  // Controlled_Buffer controlled_buffer_11
  or or_10 (or_10_out, or_3_out, updatepointerleft_1_updcli);
  assign controlled_buffer_2_out = updatepointerleft_1_updcli ? updatepointerleft_1_cli : 8'bz;  // Controlled_Buffer controlled_buffer_12
  or or_11 (or_11_out, or_4_out, updatepointerleft_1_updexp);
  assign controlled_buffer_3_out = updatepointerleft_1_updexp ? updatepointerleft_1_newvalue : 12'bz;  // Controlled_Buffer controlled_buffer_13
  UpdatePointerRight updatepointerright_1 (
    .ActivationSignal(decoder_1_out4), .Clock(Clock), .UniqueNodeID(UniqueNodeID), .PIB(PIB),
    .InternalExpression(InternalExpression), .PEB(PEB), .UpdCLE(updatepointerright_1_updcle),
    .UpdCRE(updatepointerright_1_updcre), .UpdCLI(updatepointerright_1_updcli),
    .UpdCRI(updatepointerright_1_updcri), .UpdEXP(updatepointerright_1_updexp),
    .CRI(updatepointerright_1_cri), .CLI(updatepointerright_1_cli), .CRI_2(updatepointerright_1_cri_2),
    .CLI_2(updatepointerright_1_cli_2), .NewValue(updatepointerright_1_newvalue));
  or or_12 (or_12_out, or_6_out, updatepointerright_1_updexp);
  or or_13 (or_13_out, or_7_out, updatepointerright_1_updcre);
  assign controlled_buffer_4_out = updatepointerright_1_updcre ? updatepointerright_1_cri_2 : 12'bz;  // Controlled_Buffer controlled_buffer_14
  or or_14 (or_14_out, or_8_out, updatepointerright_1_updcri);
  assign controlled_buffer_1_out = updatepointerright_1_updcri ? updatepointerright_1_cri : 8'bz;  // Controlled_Buffer controlled_buffer_15
  or or_15 (or_15_out, or_9_out, updatepointerright_1_updcle);
  assign controlled_buffer_6_out = updatepointerright_1_updcle ? updatepointerright_1_cli_2 : 12'bz;  // Controlled_Buffer controlled_buffer_16
  or or_16 (or_16_out, or_10_out, updatepointerright_1_updcli);
  assign controlled_buffer_2_out = updatepointerright_1_updcli ? updatepointerright_1_cli : 8'bz;  // Controlled_Buffer controlled_buffer_17
  or or_17 (or_17_out, or_11_out, updatepointerright_1_updexp);
  assign controlled_buffer_3_out = updatepointerright_1_updexp ? updatepointerright_1_newvalue : 12'bz;  // Controlled_Buffer controlled_buffer_18
  assign controlled_buffer_19_out = returnexpression_1_retpeb ? returnexpression_1_peb : 12'bz;  // Controlled_Buffer controlled_buffer_19
  assign controlled_buffer_20_out = returnexpression_1_retpib ? returnexpression_1_pib_2 : 8'bz;  // Controlled_Buffer controlled_buffer_20
  or or_18 (or_18_out, or_14_out, returnexpression_1_retcri);
  assign controlled_buffer_1_out = returnexpression_1_retcri ? returnexpression_1_cri_2 : 8'bz;  // Controlled_Buffer controlled_buffer_21
  ReturnExpression returnexpression_1 (
    .ActivationSignal(decoder_1_out5), .UniqueNodeID(UniqueNodeID), .PIB(PIB), .CLI(CLI), .CRI(CRI),
    .CRE(CRE), .CLE(CLE), .InternalExpression(InternalExpression), .RetCLI(returnexpression_1_retcli),
    .RetCRI(returnexpression_1_retcri), .RetPIB(returnexpression_1_retpib),
    .RetPEB(returnexpression_1_retpeb), .CRI_2(returnexpression_1_cri_2), .CLI_2(returnexpression_1_cli_2),
    .PEB(returnexpression_1_peb), .PIB_2(returnexpression_1_pib_2));
  or or_19 (or_19_out, or_16_out, returnexpression_1_retcli);
  assign controlled_buffer_2_out = returnexpression_1_retcli ? returnexpression_1_cli_2 : 8'bz;  // Controlled_Buffer controlled_buffer_22
  CompareValue comparevalue_1 (
    .ActivationSignal(decoder_1_out6), .Clock(Clock),
    .Clear(preparefortransformationasdecendantinput_1_ptdcomparevalueclear),
    .InternalValue(InternalExpression), .PEB(PEB), .PIB(PIB), .CRI(CRI), .CLI(CLI),
    .ComCLI(comparevalue_1_comcli), .ComCLE(comparevalue_1_comcle), .ComCRI(comparevalue_1_comcri),
    .ComCRE(comparevalue_1_comcre), .ComPIB(comparevalue_1_compib),
    .MarkForTransformation(comparevalue_1_markfortransformation), .CLI_2(comparevalue_1_cli_2),
    .CRI_2(comparevalue_1_cri_2), .CLE(comparevalue_1_cle), .CRE(comparevalue_1_cre),
    .PIB_2(comparevalue_1_pib_2));
  or or_20 (or_20_out, returnexpression_1_retpib, comparevalue_1_compib);
  assign controlled_buffer_20_out = comparevalue_1_compib ? comparevalue_1_pib_2 : 8'bz;  // Controlled_Buffer controlled_buffer_23
  or or_21 (or_21_out, or_13_out, comparevalue_1_comcre);
  assign controlled_buffer_4_out = comparevalue_1_comcre ? comparevalue_1_cre : 12'bz;  // Controlled_Buffer controlled_buffer_24
  or or_22 (or_22_out, or_18_out, comparevalue_1_comcri);
  assign controlled_buffer_1_out = comparevalue_1_comcri ? comparevalue_1_cri_2 : 8'bz;  // Controlled_Buffer controlled_buffer_25
  or or_23 (or_23_out, or_15_out, comparevalue_1_comcle);
  assign controlled_buffer_6_out = comparevalue_1_comcle ? comparevalue_1_cle : 12'bz;  // Controlled_Buffer controlled_buffer_26
  or or_24 (or_24_out, or_19_out, comparevalue_1_comcli);
  assign controlled_buffer_2_out = comparevalue_1_comcli ? comparevalue_1_cli_2 : 8'bz;  // Controlled_Buffer controlled_buffer_27
  or or_25 (or_25_out, or_12_out, preparefortransformationasdecendantinput_1_ptdexp);
  or or_26 (or_26_out, or_20_out, preparefortransformationasdecendantinput_1_ptdpib);
  assign controlled_buffer_20_out = preparefortransformationasdecendantinput_1_ptdpib ? preparefortransformationasdecendantinput_1_pib_2 : 8'bz;  // Controlled_Buffer controlled_buffer_28
  or or_27 (or_27_out, or_21_out, preparefortransformationasdecendantinput_1_ptdcre);
  assign controlled_buffer_4_out = preparefortransformationasdecendantinput_1_ptdcre ? preparefortransformationasdecendantinput_1_cre : 12'bz;  // Controlled_Buffer controlled_buffer_29
  PrepareForTransformationAsDecendantInput preparefortransformationasdecendantinput_1 (
    .ActivationSignal(decoder_1_out9), .Clock(Clock), .TransformMark(comparevalue_1_markfortransformation),
    .InExp(InternalExpression), .SFS(SFS), .SBS(SBS), .UniqueNodeID(UniqueNodeID), .RAM(RAM),
    .NewNodeID(NewNodeID), .PIB(PIB), .Buffer(Buffer), .PEB(PEB), .CLI(CLI), .CRI(CRI),
    .ptdCLC(preparefortransformationasdecendantinput_1_ptdclc),
    .ptdRAM(preparefortransformationasdecendantinput_1_ptdram),
    .ptdSFS(preparefortransformationasdecendantinput_1_ptdsfs),
    .ptdSEL(preparefortransformationasdecendantinput_1_ptdsel),
    .ptdNEW(preparefortransformationasdecendantinput_1_ptdnew),
    .PtdBUF(preparefortransformationasdecendantinput_1_ptdbuf),
    .ptdCRI(preparefortransformationasdecendantinput_1_ptdcri),
    .ptdCLI(preparefortransformationasdecendantinput_1_ptdcli),
    .ptdCRE(preparefortransformationasdecendantinput_1_ptdcre),
    .ptdCLE(preparefortransformationasdecendantinput_1_ptdcle),
    .PtdEXP(preparefortransformationasdecendantinput_1_ptdexp),
    .ptdSBS(preparefortransformationasdecendantinput_1_ptdsbs),
    .ptdPIB(preparefortransformationasdecendantinput_1_ptdpib),
    .ptdStackclear(preparefortransformationasdecendantinput_1_ptdstackclear),
    .ptdCompareValueClear(preparefortransformationasdecendantinput_1_ptdcomparevalueclear),
    .Output(preparefortransformationasdecendantinput_1_output),
    .CLI_2(preparefortransformationasdecendantinput_1_cli_2),
    .CLE(preparefortransformationasdecendantinput_1_cle),
    .CRI_2(preparefortransformationasdecendantinput_1_cri_2),
    .CRE(preparefortransformationasdecendantinput_1_cre),
    .PIB_2(preparefortransformationasdecendantinput_1_pib_2),
    .NewExpression(preparefortransformationasdecendantinput_1_newexpression));  // open: PtdToggleChildren
  assign RamSelect = and_1_out ? preparefortransformationasdecendantinput_1_ptdsel : 1'bz;  // Controlled_Buffer controlled_buffer_30
  assign BackStack = and_1_out ? preparefortransformationasdecendantinput_1_ptdsbs : 1'bz;  // Controlled_Buffer controlled_buffer_31
  assign FrontStack = and_1_out ? preparefortransformationasdecendantinput_1_ptdsfs : 1'bz;  // Controlled_Buffer controlled_buffer_32
  assign RAMwrite = and_1_out ? preparefortransformationasdecendantinput_1_ptdram : 1'bz;  // Controlled_Buffer controlled_buffer_33
  assign EXPWrite = and_1_out ? or_25_out : 1'bz;  // Controlled_Buffer controlled_buffer_34
  assign NewNode = and_1_out ? preparefortransformationasdecendantinput_1_ptdnew : 1'bz;  // Controlled_Buffer controlled_buffer_35
  or or_28 (or_28_out, or_22_out, preparefortransformationasdecendantinput_1_ptdcri);
  assign controlled_buffer_1_out = preparefortransformationasdecendantinput_1_ptdcri ? preparefortransformationasdecendantinput_1_cri_2 : 8'bz;  // Controlled_Buffer controlled_buffer_36
  or or_29 (or_29_out, or_23_out, preparefortransformationasdecendantinput_1_ptdcle);
  assign controlled_buffer_6_out = preparefortransformationasdecendantinput_1_ptdcle ? preparefortransformationasdecendantinput_1_cle : 12'bz;  // Controlled_Buffer controlled_buffer_37
  or or_30 (or_30_out, or_24_out, preparefortransformationasdecendantinput_1_ptdcli);
  assign controlled_buffer_2_out = preparefortransformationasdecendantinput_1_ptdcli ? preparefortransformationasdecendantinput_1_cli_2 : 8'bz;  // Controlled_Buffer controlled_buffer_38
  or or_31 (or_31_out, or_17_out, preparefortransformationasdecendantinput_1_ptdexp);
  assign controlled_buffer_3_out = preparefortransformationasdecendantinput_1_ptdexp ? preparefortransformationasdecendantinput_1_newexpression : 12'bz;  // Controlled_Buffer controlled_buffer_39
  or or_32 (or_32_out, or_5_out, preparefortransformationasdecendantinput_1_ptdstackclear);
  or or_33 (or_33_out, preparefortransformationasdecendantinput_1_ptdram, preparefortransformationasdecendantinput_1_ptdsfs, preparefortransformationasdecendantinput_1_ptdsbs, preparefortransformationasdecendantinput_1_ptdbuf);
  assign controlled_buffer_40_out = or_33_out ? preparefortransformationasdecendantinput_1_output : 8'bz;  // Controlled_Buffer controlled_buffer_40
  BranchChop branchchop_1 (
    .Clock(Clock), .CLI(CLI), .CRI(CRI), .InternalExpression(InternalExpression),
    .BraNew(branchchop_1_branew), .NewValue(branchchop_1_newvalue));
  or or_34 (or_34_out, or_31_out, branchchop_1_branew);
  assign controlled_buffer_3_out = branchchop_1_branew ? branchchop_1_newvalue : 12'bz;  // Controlled_Buffer controlled_buffer_41
  not not_2 (not_2_out, returnexpression_1_retpeb);
  assign controlled_buffer_19_out = not_2_out ? CLE : 12'bz;  // Controlled_Buffer controlled_buffer_42
  not not_3 (not_3_out, or_26_out);
  assign controlled_buffer_20_out = not_3_out ? CRI : 8'bz;  // Controlled_Buffer controlled_buffer_43
  not not_4 (not_4_out, or_27_out);
  assign controlled_buffer_4_out = not_4_out ? PEB : 12'bz;  // Controlled_Buffer controlled_buffer_44
  not not_5 (not_5_out, or_28_out);
  assign controlled_buffer_1_out = not_5_out ? CLI : 8'bz;  // Controlled_Buffer controlled_buffer_45
  not not_6 (not_6_out, or_29_out);
  assign controlled_buffer_6_out = not_6_out ? CRE : 12'bz;  // Controlled_Buffer controlled_buffer_46
  not not_7 (not_7_out, or_30_out);
  assign controlled_buffer_2_out = not_7_out ? PIB : 8'bz;  // Controlled_Buffer controlled_buffer_47
  not not_8 (not_8_out, or_34_out);
  assign controlled_buffer_3_out = not_8_out ? {12{1'b0}} : 12'bz;  // Controlled_Buffer controlled_buffer_48
  not not_9 (not_9_out, or_33_out);
  assign controlled_buffer_40_out = not_9_out ? {8{1'b0}} : 8'bz;  // Controlled_Buffer controlled_buffer_49
  assign ClearChidlren = and_1_out ? preparefortransformationasdecendantinput_1_ptdclc : 1'bz;  // Controlled_Buffer controlled_buffer_50
  assign PEB_2 = and_1_out ? controlled_buffer_19_out : 12'bz;  // Controlled_Buffer controlled_buffer_51
  assign PIB_2 = and_1_out ? controlled_buffer_20_out : 8'bz;  // Controlled_Buffer controlled_buffer_52
  assign CRE_2 = and_1_out ? controlled_buffer_4_out : 12'bz;  // Controlled_Buffer controlled_buffer_53
  assign CRI_2 = and_1_out ? controlled_buffer_1_out : 8'bz;  // Controlled_Buffer controlled_buffer_54
  assign CLE_2 = and_1_out ? controlled_buffer_6_out : 12'bz;  // Controlled_Buffer controlled_buffer_55
  assign CLI_2 = and_1_out ? controlled_buffer_2_out : 8'bz;  // Controlled_Buffer controlled_buffer_56
  assign NewNode_2 = and_1_out ? controlled_buffer_3_out : 12'bz;  // Controlled_Buffer controlled_buffer_57
  assign GeneralOutput = and_1_out ? controlled_buffer_40_out : 8'bz;  // Controlled_Buffer controlled_buffer_58
  assign StackClear = and_1_out ? or_32_out : 1'bz;  // Controlled_Buffer controlled_buffer_59

  // Notes on the sheet:
  //   Input
  //   0 == Backstack / 1 == Frontstack
  //   Output
endmodule
module FunctionExpression (
  input  [11:0] PEB,
  input  [7:0] PIB,
  input  [11:0] CRE,
  input  [7:0] CRI,
  input  [11:0] CLE,
  input  [7:0] CLI,
  input  [3:0] SFS,
  input  [3:0] SBS,
  input  [3:0] RAM,
  input  [11:0] InternalExpression,
  input  UnreduceFlag,
  input  Clock,
  input  [3:0] NewNodeID,
  input  [3:0] UniqueNodeID,
  output EXPWrite,
  output RamSelect,
  output FrontStack,
  output BackStack,
  output RAMwrite,
  output NewNode,
  output [11:0] PEB_2,
  output [7:0] PIB_2,
  output [11:0] CRE_2,
  output [7:0] CRI_2,
  output [11:0] CLE_2,
  output [7:0] CLI_2,
  output [11:0] NewNode_2,
  output [7:0] GeneralOutput,
  output ResolveFlagOveride,
  output ClearChidlren,
  output StackClear
);

  wire and_1_out, decoder_1_out0, decoder_1_out1, decoder_1_out2, decoder_1_out3, decoder_1_out4,
       decoder_1_out5, decoder_1_out7, decoder_1_out8, functioncorelogic_1_corecre,
       functioncorelogic_1_corecri, functioncorelogic_1_corenew, functioncorelogic_1_corepib,
       immediateresolution_1_immpib, not_2_out, not_3_out, not_4_out, not_5_out, not_6_out, not_7_out,
       not_8_out, not_9_out, nullification_1_nullcli, nullification_1_nullcri, nullification_1_nullexp,
       nullification_1_nullstackclear, or_1_out, or_2_out, or_3_out, or_4_out, or_5_out, or_6_out, or_7_out,
       or_8_out, or_9_out, or_10_out, or_11_out, or_12_out, or_13_out, or_14_out, or_15_out, or_16_out,
       or_17_out, or_18_out, or_19_out, or_20_out, or_21_out, or_22_out, or_23_out, or_24_out, or_25_out,
       or_26_out, or_27_out, or_28_out, or_29_out, or_30_out,
       preparefortransformationasancestorinput_1_ptacli, preparefortransformationasancestorinput_1_ptacri,
       preparefortransformationasancestorinput_1_ptapeb, preparefortransformationasancestorinput_1_ptapib,
       preparefortransformationasancestorinput_1_ptaram, preparefortransformationasancestorinput_1_ptasbs,
       preparefortransformationasancestorinput_1_ptasel, preparefortransformationasancestorinput_1_ptasfs,
       preparefortransformationasancestorinput_1_ptastackclear, returnexpression_1_retcli,
       returnexpression_1_retcri, returnexpression_1_retpeb, returnexpression_1_retpib,
       updateexpression_1_updcle, updateexpression_1_updcli, updateexpression_1_updcre,
       updateexpression_1_updcri, updateexpression_1_updexp, updateexpression_1_updstackclear,
       updatepointerleft_1_updcle, updatepointerleft_1_updcli, updatepointerleft_1_updcre,
       updatepointerleft_1_updcri, updatepointerleft_1_updexp, updatepointerright_1_updcle,
       updatepointerright_1_updcli, updatepointerright_1_updcre, updatepointerright_1_updcri,
       updatepointerright_1_updexp;
  wire [2:0] not_1_out, xor_1_out;
  wire [7:0] controlled_buffer_1_out, controlled_buffer_3_out, controlled_buffer_6_out,
       controlled_buffer_45_out, functioncorelogic_1_cri_2, functioncorelogic_1_pib,
       immediateresolution_1_out_3, nullification_1_cli, nullification_1_cri,
       preparefortransformationasancestorinput_1_cli_2, preparefortransformationasancestorinput_1_cri_2,
       preparefortransformationasancestorinput_1_generalouput, preparefortransformationasancestorinput_1_pib,
       returnexpression_1_cli_2, returnexpression_1_cri_2, returnexpression_1_pib_2, updateexpression_1_cli,
       updateexpression_1_cri, updatepointerleft_1_cli, updatepointerleft_1_cri, updatepointerright_1_cli,
       updatepointerright_1_cri;
  wire [11:0] controlled_buffer_2_out, controlled_buffer_4_out, controlled_buffer_10_out,
       controlled_buffer_23_out, functioncorelogic_1_cre, functioncorelogic_1_new, nullification_1_newvalue,
       preparefortransformationasancestorinput_1_peb, returnexpression_1_peb, updateexpression_1_cle,
       updateexpression_1_cre, updateexpression_1_newvalue, updatepointerleft_1_cle, updatepointerleft_1_cre,
       updatepointerleft_1_newvalue, updatepointerright_1_cli_2, updatepointerright_1_cri_2,
       updatepointerright_1_newvalue;

  Decoder #(.select(4)) decoder_1 (
    .out0(decoder_1_out0), .out1(decoder_1_out1), .out2(decoder_1_out2), .out3(decoder_1_out3),
    .out4(decoder_1_out4), .out5(decoder_1_out5), .out7(decoder_1_out7), .out8(decoder_1_out8), .sel(PIB[7:4]));  // open: out6, out9, out10, out11, out12, out13, out14, out15, en
  assign controlled_buffer_1_out = functioncorelogic_1_corepib ? functioncorelogic_1_pib : 8'bz;  // Controlled_Buffer controlled_buffer_1
  FunctionCoreLogic functioncorelogic_1 (
    .ActivationSignal(decoder_1_out0), .UnreduceableFlag(UnreduceFlag), .Clock(Clock), .PEB(PEB),
    .InternalExpression(InternalExpression), .CLE(CLE), .CRI(CRI), .CoreCRI(functioncorelogic_1_corecri),
    .CoreCRE(functioncorelogic_1_corecre), .CorePIB(functioncorelogic_1_corepib),
    .CoreNew(functioncorelogic_1_corenew), .CRE(functioncorelogic_1_cre), .CRI_2(functioncorelogic_1_cri_2),
    .PIB(functioncorelogic_1_pib), .New(functioncorelogic_1_new));
  assign xor_1_out = InternalExpression[10:8] ^ 3'b011;  // XOR_Gate xor_1, 3 bits wide
  assign not_1_out = ~xor_1_out;  // NOT_Gate not_1, 3 bits wide
  assign controlled_buffer_2_out = functioncorelogic_1_corecre ? functioncorelogic_1_cre : 12'bz;  // Controlled_Buffer controlled_buffer_2
  assign controlled_buffer_3_out = functioncorelogic_1_corecri ? functioncorelogic_1_cri_2 : 8'bz;  // Controlled_Buffer controlled_buffer_3
  assign controlled_buffer_4_out = functioncorelogic_1_corenew ? functioncorelogic_1_new : 12'bz;  // Controlled_Buffer controlled_buffer_4
  or or_1 (or_1_out, functioncorelogic_1_corecri, nullification_1_nullcli);
  assign controlled_buffer_3_out = nullification_1_nullcli ? nullification_1_cri : 8'bz;  // Controlled_Buffer controlled_buffer_5
  assign controlled_buffer_6_out = nullification_1_nullcri ? nullification_1_cli : 8'bz;  // Controlled_Buffer controlled_buffer_6
  or or_2 (or_2_out, functioncorelogic_1_corenew, nullification_1_nullexp);
  assign controlled_buffer_4_out = nullification_1_nullexp ? nullification_1_newvalue : 12'bz;  // Controlled_Buffer controlled_buffer_7
  Nullification nullification_1 (
    .ActivationSignal(decoder_1_out1), .Clock(Clock), .NullCLI(nullification_1_nullcli),
    .NullCRI(nullification_1_nullcri), .NullStackClear(nullification_1_nullstackclear),
    .NullEXP(nullification_1_nullexp), .CRI(nullification_1_cri), .CLI(nullification_1_cli),
    .NewValue(nullification_1_newvalue));
  and and_1 (and_1_out, not_1_out[0], not_1_out[1], not_1_out[2]);
  UpdateExpression updateexpression_1 (
    .ActivationSignal(decoder_1_out2), .Clock(Clock), .UniqueNodeID(UniqueNodeID), .PIB(PIB), .PEB(PEB),
    .UpdCLE(updateexpression_1_updcle), .UpdCRE(updateexpression_1_updcre),
    .UpdCLI(updateexpression_1_updcli), .UpdCRI(updateexpression_1_updcri),
    .UpdStackClear(updateexpression_1_updstackclear), .UpdEXP(updateexpression_1_updexp),
    .CRI(updateexpression_1_cri), .CLI(updateexpression_1_cli), .CRE(updateexpression_1_cre),
    .CLE(updateexpression_1_cle), .NewValue(updateexpression_1_newvalue));
  or or_3 (or_3_out, nullification_1_nullexp, updateexpression_1_updexp);
  or or_4 (or_4_out, functioncorelogic_1_corecre, updateexpression_1_updcre);
  assign controlled_buffer_2_out = updateexpression_1_updcre ? updateexpression_1_cre : 12'bz;  // Controlled_Buffer controlled_buffer_8
  or or_5 (or_5_out, or_1_out, updateexpression_1_updcri);
  assign controlled_buffer_3_out = updateexpression_1_updcri ? updateexpression_1_cri : 8'bz;  // Controlled_Buffer controlled_buffer_9
  assign controlled_buffer_10_out = updateexpression_1_updcle ? updateexpression_1_cle : 12'bz;  // Controlled_Buffer controlled_buffer_10
  or or_6 (or_6_out, nullification_1_nullcri, updateexpression_1_updcli);
  assign controlled_buffer_6_out = updateexpression_1_updcli ? updateexpression_1_cli : 8'bz;  // Controlled_Buffer controlled_buffer_11
  or or_7 (or_7_out, or_2_out, updateexpression_1_updexp);
  assign controlled_buffer_4_out = updateexpression_1_updexp ? updateexpression_1_newvalue : 12'bz;  // Controlled_Buffer controlled_buffer_12
  or or_8 (or_8_out, nullification_1_nullstackclear, updateexpression_1_updstackclear);
  or or_9 (or_9_out, or_3_out, updatepointerleft_1_updexp);
  or or_10 (or_10_out, or_4_out, updatepointerleft_1_updcre);
  assign controlled_buffer_2_out = updatepointerleft_1_updcre ? updatepointerleft_1_cre : 12'bz;  // Controlled_Buffer controlled_buffer_13
  or or_11 (or_11_out, or_5_out, updatepointerleft_1_updcri);
  assign controlled_buffer_3_out = updatepointerleft_1_updcri ? updatepointerleft_1_cri : 8'bz;  // Controlled_Buffer controlled_buffer_14
  or or_12 (or_12_out, updateexpression_1_updcle, updatepointerleft_1_updcle);
  assign controlled_buffer_10_out = updatepointerleft_1_updcle ? updatepointerleft_1_cle : 12'bz;  // Controlled_Buffer controlled_buffer_15
  or or_13 (or_13_out, or_6_out, updatepointerleft_1_updcli);
  assign controlled_buffer_6_out = updatepointerleft_1_updcli ? updatepointerleft_1_cli : 8'bz;  // Controlled_Buffer controlled_buffer_16
  UpdatePointerLeft updatepointerleft_1 (
    .ActivationSignal(decoder_1_out3), .Clock(Clock), .UniqueNodeID(UniqueNodeID), .PIB(PIB),
    .InternalExpression(InternalExpression), .PEB(PEB), .UpdCLE(updatepointerleft_1_updcle),
    .UpdCRE(updatepointerleft_1_updcre), .UpdCLI(updatepointerleft_1_updcli),
    .UpdCRI(updatepointerleft_1_updcri), .UpdEXP(updatepointerleft_1_updexp), .CRI(updatepointerleft_1_cri),
    .CLI(updatepointerleft_1_cli), .CRE(updatepointerleft_1_cre), .CLE(updatepointerleft_1_cle),
    .NewValue(updatepointerleft_1_newvalue));
  or or_14 (or_14_out, or_7_out, updatepointerleft_1_updexp);
  assign controlled_buffer_4_out = updatepointerleft_1_updexp ? updatepointerleft_1_newvalue : 12'bz;  // Controlled_Buffer controlled_buffer_17
  or or_15 (or_15_out, or_9_out, updatepointerright_1_updexp);
  or or_16 (or_16_out, or_10_out, updatepointerright_1_updcre);
  assign controlled_buffer_2_out = updatepointerright_1_updcre ? updatepointerright_1_cri_2 : 12'bz;  // Controlled_Buffer controlled_buffer_18
  or or_17 (or_17_out, or_11_out, updatepointerright_1_updcri);
  assign controlled_buffer_3_out = updatepointerright_1_updcri ? updatepointerright_1_cri : 8'bz;  // Controlled_Buffer controlled_buffer_19
  or or_18 (or_18_out, or_12_out, updatepointerright_1_updcle);
  assign controlled_buffer_10_out = updatepointerright_1_updcle ? updatepointerright_1_cli_2 : 12'bz;  // Controlled_Buffer controlled_buffer_20
  UpdatePointerRight updatepointerright_1 (
    .ActivationSignal(decoder_1_out4), .Clock(Clock), .UniqueNodeID(UniqueNodeID), .PIB(PIB),
    .InternalExpression(InternalExpression), .PEB(PEB), .UpdCLE(updatepointerright_1_updcle),
    .UpdCRE(updatepointerright_1_updcre), .UpdCLI(updatepointerright_1_updcli),
    .UpdCRI(updatepointerright_1_updcri), .UpdEXP(updatepointerright_1_updexp),
    .CRI(updatepointerright_1_cri), .CLI(updatepointerright_1_cli), .CRI_2(updatepointerright_1_cri_2),
    .CLI_2(updatepointerright_1_cli_2), .NewValue(updatepointerright_1_newvalue));
  or or_19 (or_19_out, or_13_out, updatepointerright_1_updcli);
  assign controlled_buffer_6_out = updatepointerright_1_updcli ? updatepointerright_1_cli : 8'bz;  // Controlled_Buffer controlled_buffer_21
  or or_20 (or_20_out, or_14_out, updatepointerright_1_updexp);
  assign controlled_buffer_4_out = updatepointerright_1_updexp ? updatepointerright_1_newvalue : 12'bz;  // Controlled_Buffer controlled_buffer_22
  assign controlled_buffer_23_out = returnexpression_1_retpeb ? returnexpression_1_peb : 12'bz;  // Controlled_Buffer controlled_buffer_23
  ReturnExpression returnexpression_1 (
    .ActivationSignal(decoder_1_out5), .UniqueNodeID(UniqueNodeID), .PIB(PIB), .CLI(CLI), .CRI(CRI),
    .CRE(CRE), .CLE(CLE), .InternalExpression(InternalExpression), .RetCLI(returnexpression_1_retcli),
    .RetCRI(returnexpression_1_retcri), .RetPIB(returnexpression_1_retpib),
    .RetPEB(returnexpression_1_retpeb), .CRI_2(returnexpression_1_cri_2), .CLI_2(returnexpression_1_cli_2),
    .PEB(returnexpression_1_peb), .PIB_2(returnexpression_1_pib_2));
  or or_21 (or_21_out, functioncorelogic_1_corepib, returnexpression_1_retpib);
  assign controlled_buffer_1_out = returnexpression_1_retpib ? returnexpression_1_pib_2 : 8'bz;  // Controlled_Buffer controlled_buffer_24
  or or_22 (or_22_out, or_17_out, returnexpression_1_retcri);
  assign controlled_buffer_3_out = returnexpression_1_retcri ? returnexpression_1_cri_2 : 8'bz;  // Controlled_Buffer controlled_buffer_25
  or or_23 (or_23_out, or_19_out, returnexpression_1_retcli);
  assign controlled_buffer_6_out = returnexpression_1_retcli ? returnexpression_1_cli_2 : 8'bz;  // Controlled_Buffer controlled_buffer_26
  ImmediateResolution immediateresolution_1 (
    .ActivationSignal(decoder_1_out7), .ImmPIB(immediateresolution_1_immpib),
    .out_3(immediateresolution_1_out_3));
  or or_24 (or_24_out, or_21_out, immediateresolution_1_immpib);
  assign controlled_buffer_1_out = immediateresolution_1_immpib ? immediateresolution_1_out_3 : 8'bz;  // Controlled_Buffer controlled_buffer_27
  assign RamSelect = and_1_out ? preparefortransformationasancestorinput_1_ptasel : 1'bz;  // Controlled_Buffer controlled_buffer_28
  assign BackStack = and_1_out ? preparefortransformationasancestorinput_1_ptasbs : 1'bz;  // Controlled_Buffer controlled_buffer_29
  assign FrontStack = and_1_out ? preparefortransformationasancestorinput_1_ptasfs : 1'bz;  // Controlled_Buffer controlled_buffer_30
  assign RAMwrite = and_1_out ? preparefortransformationasancestorinput_1_ptaram : 1'bz;  // Controlled_Buffer controlled_buffer_31
  assign EXPWrite = and_1_out ? or_15_out : 1'bz;  // Controlled_Buffer controlled_buffer_32
  assign NewNode = and_1_out ? preparefortransformationasancestorinput_1_ptasbs : 1'bz;  // Controlled_Buffer controlled_buffer_33
  PrepareForTransformationAsAncestorInput preparefortransformationasancestorinput_1 (
    .ActivationSignal(decoder_1_out8), .Clock(Clock), .SFS(SFS), .SBS(SBS), .RAM(RAM),
    .UniqueNodeID(UniqueNodeID), .CLI(CLI), .CRI(CRI), .CLE(CLE), .CRE(CRE),
    .InternalExpression(InternalExpression), .ptaRAM(preparefortransformationasancestorinput_1_ptaram),
    .ptaSFS(preparefortransformationasancestorinput_1_ptasfs),
    .ptaPEB(preparefortransformationasancestorinput_1_ptapeb),
    .ptaCLI(preparefortransformationasancestorinput_1_ptacli),
    .ptaCRI(preparefortransformationasancestorinput_1_ptacri),
    .ptaSEL(preparefortransformationasancestorinput_1_ptasel),
    .ptaSBS(preparefortransformationasancestorinput_1_ptasbs),
    .ptaStackClear(preparefortransformationasancestorinput_1_ptastackclear),
    .ptaPIB(preparefortransformationasancestorinput_1_ptapib),
    .GeneralOuput(preparefortransformationasancestorinput_1_generalouput),
    .PEB(preparefortransformationasancestorinput_1_peb),
    .CLI_2(preparefortransformationasancestorinput_1_cli_2),
    .CRI_2(preparefortransformationasancestorinput_1_cri_2),
    .PIB(preparefortransformationasancestorinput_1_pib));
  or or_25 (or_25_out, returnexpression_1_retpeb, preparefortransformationasancestorinput_1_ptapeb);
  not not_2 (not_2_out, or_25_out);
  assign controlled_buffer_23_out = preparefortransformationasancestorinput_1_ptapeb ? preparefortransformationasancestorinput_1_peb : 12'bz;  // Controlled_Buffer controlled_buffer_34
  or or_26 (or_26_out, or_24_out, preparefortransformationasancestorinput_1_ptapib);
  not not_3 (not_3_out, or_26_out);
  assign controlled_buffer_1_out = preparefortransformationasancestorinput_1_ptapib ? preparefortransformationasancestorinput_1_pib : 8'bz;  // Controlled_Buffer controlled_buffer_35
  not not_4 (not_4_out, or_16_out);
  or or_27 (or_27_out, or_22_out, preparefortransformationasancestorinput_1_ptacri);
  not not_5 (not_5_out, or_27_out);
  assign controlled_buffer_3_out = preparefortransformationasancestorinput_1_ptacri ? preparefortransformationasancestorinput_1_cri_2 : 8'bz;  // Controlled_Buffer controlled_buffer_36
  not not_6 (not_6_out, or_18_out);
  or or_28 (or_28_out, or_23_out, preparefortransformationasancestorinput_1_ptacli);
  not not_7 (not_7_out, or_28_out);
  assign controlled_buffer_6_out = preparefortransformationasancestorinput_1_ptacli ? preparefortransformationasancestorinput_1_cli_2 : 8'bz;  // Controlled_Buffer controlled_buffer_37
  not not_8 (not_8_out, or_20_out);
  or or_29 (or_29_out, or_8_out, preparefortransformationasancestorinput_1_ptastackclear);
  or or_30 (or_30_out, preparefortransformationasancestorinput_1_ptaram, preparefortransformationasancestorinput_1_ptasfs, preparefortransformationasancestorinput_1_ptasbs);
  and and_2 (ResolveFlagOveride, and_1_out, UnreduceFlag);
  assign controlled_buffer_23_out = not_2_out ? InternalExpression : 12'bz;  // Controlled_Buffer controlled_buffer_38
  assign controlled_buffer_1_out = not_3_out ? {8{1'b0}} : 8'bz;  // Controlled_Buffer controlled_buffer_39
  assign controlled_buffer_2_out = not_4_out ? {12{1'b0}} : 12'bz;  // Controlled_Buffer controlled_buffer_40
  assign controlled_buffer_3_out = not_5_out ? {8{1'b0}} : 8'bz;  // Controlled_Buffer controlled_buffer_41
  assign controlled_buffer_10_out = not_6_out ? {12{1'b0}} : 12'bz;  // Controlled_Buffer controlled_buffer_42
  assign controlled_buffer_6_out = not_7_out ? {8{1'b0}} : 8'bz;  // Controlled_Buffer controlled_buffer_43
  assign controlled_buffer_4_out = not_8_out ? {12{1'b0}} : 12'bz;  // Controlled_Buffer controlled_buffer_44
  assign controlled_buffer_45_out = or_30_out ? preparefortransformationasancestorinput_1_generalouput : 8'bz;  // Controlled_Buffer controlled_buffer_45
  not not_9 (not_9_out, or_30_out);
  assign controlled_buffer_45_out = not_9_out ? {8{1'b0}} : 8'bz;  // Controlled_Buffer controlled_buffer_46
  assign ClearChidlren = and_1_out ? 1'b0 : 1'bz;  // Controlled_Buffer controlled_buffer_47
  assign PEB_2 = and_1_out ? controlled_buffer_23_out : 12'bz;  // Controlled_Buffer controlled_buffer_48
  assign PIB_2 = and_1_out ? controlled_buffer_1_out : 8'bz;  // Controlled_Buffer controlled_buffer_49
  assign CRE_2 = and_1_out ? controlled_buffer_2_out : 12'bz;  // Controlled_Buffer controlled_buffer_50
  assign CRI_2 = and_1_out ? controlled_buffer_3_out : 8'bz;  // Controlled_Buffer controlled_buffer_51
  assign CLE_2 = and_1_out ? controlled_buffer_10_out : 12'bz;  // Controlled_Buffer controlled_buffer_52
  assign CLI_2 = and_1_out ? controlled_buffer_6_out : 8'bz;  // Controlled_Buffer controlled_buffer_53
  assign NewNode_2 = and_1_out ? controlled_buffer_4_out : 12'bz;  // Controlled_Buffer controlled_buffer_54
  assign GeneralOutput = and_1_out ? controlled_buffer_45_out : 8'bz;  // Controlled_Buffer controlled_buffer_55
  assign StackClear = and_1_out ? or_29_out : 1'bz;  // Controlled_Buffer controlled_buffer_56
  // also tied to GND on the sheet: preparefortransformationasancestorinput_1_ptasbs

  // Notes on the sheet:
  //   Input
  //   0 == Backstack / 1 == Frontstack
  //   Output
endmodule

module Nullification (
  input  ActivationSignal,
  input  Clock,
  output NullCLI,
  output NullStackClear,
  output NullCRI,
  output NullEXP,
  output [7:0] CRI,
  output [7:0] CLI,
  output [11:0] NewValue
);

  wire and_1_out, d_ff_1_q, not_1_out, or_2_out;

  or or_1 (NullCLI, and_1_out, NullEXP);
  not not_1 (not_1_out, NullEXP);
  D_Flip_Flop d_ff_1 (.D(and_1_out), .clk(Clock), .Q(d_ff_1_q));  // open: Qn, preset, reset
  and and_1 (and_1_out, ActivationSignal, not_1_out);
  or or_2 (or_2_out, and_1_out, NullEXP);
  assign CLI = or_2_out ? 8'h10 : 8'bz;  // Controlled_Buffer controlled_buffer_1
  and and_2 (NullEXP, ActivationSignal, d_ff_1_q);
  assign NewValue = NullEXP ? {12{1'b0}} : 12'bz;  // Controlled_Buffer controlled_buffer_2

  assign CRI = CLI;
  assign NullCRI = NullCLI;
  assign NullStackClear = NullEXP;
endmodule

module UpdateExpression (
  input  ActivationSignal,
  input  Clock,
  input  [3:0] UniqueNodeID,
  input  [7:0] PIB,
  input  [11:0] PEB,
  output UpdCLE,
  output UpdCRE,
  output UpdStackClear,
  output UpdCLI,
  output UpdEXP,
  output UpdCRI,
  output [7:0] CRI,
  output [7:0] CLI,
  output [11:0] CRE,
  output [11:0] CLE,
  output [11:0] NewValue
);

  wire and_1_out, and_2_out, and_3_out, and_5_out, d_ff_1_q, not_1_out, or_2_out;
  wire [3:0] not_2_out, xor_1_out;

  not not_1 (not_1_out, and_2_out);
  and and_1 (and_1_out, ActivationSignal, not_1_out);
  assign CLI = or_2_out ? PIB : 8'bz;  // Controlled_Buffer controlled_buffer_1
  assign CLE = or_2_out ? PEB : 12'bz;  // Controlled_Buffer controlled_buffer_2
  or or_1 (UpdCLE, and_1_out, and_2_out);
  D_Flip_Flop d_ff_1 (.D(and_1_out), .clk(Clock), .Q(d_ff_1_q));  // open: Qn, preset, reset
  or or_2 (or_2_out, and_1_out, and_2_out);
  assign xor_1_out = UniqueNodeID ^ PIB[3:0];  // XOR_Gate xor_1, 4 bits wide
  and and_2 (and_2_out, ActivationSignal, d_ff_1_q);
  and and_3 (and_3_out, not_2_out[0], not_2_out[1], not_2_out[2], not_2_out[3]);
  assign not_2_out = ~xor_1_out;  // NOT_Gate not_2, 4 bits wide
  and and_4 (UpdEXP, and_3_out, and_2_out);
  and and_5 (and_5_out, and_3_out, and_2_out);
  assign NewValue = and_5_out ? {1'b0, PEB[10:0]} : 12'bz;  // Controlled_Buffer controlled_buffer_3

  assign CRE = CLE;
  assign CRI = CLI;
  assign UpdCLI = UpdCLE;
  assign UpdCRE = UpdCLE;
  assign UpdCRI = UpdCLE;
  assign UpdStackClear = UpdEXP;
endmodule

module UpdatePointerLeft (
  input  ActivationSignal,
  input  Clock,
  input  [3:0] UniqueNodeID,
  input  [7:0] PIB,
  input  [11:0] InternalExpression,
  input  [11:0] PEB,
  output UpdCLE,
  output UpdCRE,
  output UpdCLI,
  output UpdEXP,
  output UpdCRI,
  output [7:0] CRI,
  output [7:0] CLI,
  output [11:0] CRE,
  output [11:0] CLE,
  output [11:0] NewValue
);

  wire and_1_out, and_2_out, and_3_out, and_5_out, d_ff_1_q, not_1_out, or_2_out;
  wire [3:0] not_2_out, xor_1_out;

  not not_1 (not_1_out, and_2_out);
  and and_1 (and_1_out, ActivationSignal, not_1_out);
  assign CLI = or_2_out ? PIB : 8'bz;  // Controlled_Buffer controlled_buffer_1
  assign CLE = or_2_out ? PEB : 12'bz;  // Controlled_Buffer controlled_buffer_2
  or or_1 (UpdCLE, and_1_out, and_2_out);
  D_Flip_Flop d_ff_1 (.D(and_1_out), .clk(Clock), .Q(d_ff_1_q));  // open: Qn, preset, reset
  or or_2 (or_2_out, and_1_out, and_2_out);
  assign xor_1_out = UniqueNodeID ^ PIB[3:0];  // XOR_Gate xor_1, 4 bits wide
  and and_2 (and_2_out, ActivationSignal, d_ff_1_q);
  and and_3 (and_3_out, not_2_out[0], not_2_out[1], not_2_out[2], not_2_out[3]);
  assign not_2_out = ~xor_1_out;  // NOT_Gate not_2, 4 bits wide
  and and_4 (UpdEXP, and_3_out, and_2_out);
  and and_5 (and_5_out, and_3_out, and_2_out);
  assign NewValue = and_5_out ? {InternalExpression[11:8], PEB[7:4], InternalExpression[3:0]} : 12'bz;  // Controlled_Buffer controlled_buffer_3

  assign CRE = CLE;
  assign CRI = CLI;
  assign UpdCLI = UpdCLE;
  assign UpdCRE = UpdCLE;
  assign UpdCRI = UpdCLE;
endmodule

module UpdatePointerRight (
  input  ActivationSignal,
  input  Clock,
  input  [3:0] UniqueNodeID,
  input  [7:0] PIB,
  input  [11:0] InternalExpression,
  input  [11:0] PEB,
  output UpdCLE,
  output UpdCRE,
  output UpdCLI,
  output UpdEXP,
  output UpdCRI,
  output [7:0] CRI,
  output [7:0] CLI,
  output [11:0] CRI_2,
  output [11:0] CLI_2,
  output [11:0] NewValue
);

  wire and_1_out, and_2_out, and_3_out, and_5_out, d_ff_1_q, not_1_out, or_2_out;
  wire [3:0] not_2_out, xor_1_out;

  not not_1 (not_1_out, and_2_out);
  and and_1 (and_1_out, ActivationSignal, not_1_out);
  assign CLI = or_2_out ? PIB : 8'bz;  // Controlled_Buffer controlled_buffer_1
  assign CLI_2 = or_2_out ? PEB : 12'bz;  // Controlled_Buffer controlled_buffer_2
  or or_1 (UpdCLE, and_1_out, and_2_out);
  D_Flip_Flop d_ff_1 (.D(and_1_out), .clk(Clock), .Q(d_ff_1_q));  // open: Qn, preset, reset
  or or_2 (or_2_out, and_1_out, and_2_out);
  assign xor_1_out = UniqueNodeID ^ PIB[3:0];  // XOR_Gate xor_1, 4 bits wide
  and and_2 (and_2_out, ActivationSignal, d_ff_1_q);
  and and_3 (and_3_out, not_2_out[0], not_2_out[1], not_2_out[2], not_2_out[3]);
  assign not_2_out = ~xor_1_out;  // NOT_Gate not_2, 4 bits wide
  and and_4 (UpdEXP, and_3_out, and_2_out);
  and and_5 (and_5_out, and_3_out, and_2_out);
  assign NewValue = and_5_out ? {InternalExpression[11:4], PEB[3:0]} : 12'bz;  // Controlled_Buffer controlled_buffer_3

  assign CRI = CLI;
  assign CRI_2 = CLI_2;
  assign UpdCLI = UpdCLE;
  assign UpdCRE = UpdCLE;
  assign UpdCRI = UpdCLE;
endmodule

module ReturnExpression (
  input  ActivationSignal,
  input  [3:0] UniqueNodeID,
  input  [7:0] PIB,
  input  [7:0] CLI,
  input  [7:0] CRI,
  input  [11:0] CRE,
  input  [11:0] CLE,
  input  [11:0] InternalExpression,
  output RetPIB,
  output RetCLI,
  output RetPEB,
  output RetCRI,
  output [7:0] CRI_2,
  output [7:0] CLI_2,
  output [11:0] PEB,
  output [7:0] PIB_2
);

  wire and_1_out, and_2_out, and_3_out, and_5_out, and_6_out, and_7_out, or_1_out, or_2_out;
  wire [3:0] not_1_out, not_2_out, not_3_out, xor_1_out, xor_2_out, xor_3_out;

  assign xor_1_out = UniqueNodeID ^ PIB[3:0];  // XOR_Gate xor_1, 4 bits wide
  assign not_1_out = ~xor_1_out;  // NOT_Gate not_1, 4 bits wide
  assign CLI_2 = ActivationSignal ? PIB : 8'bz;  // Controlled_Buffer controlled_buffer_1
  assign xor_2_out = 4'b0011 ^ CLI[7:4];  // XOR_Gate xor_2, 4 bits wide
  assign not_2_out = ~xor_2_out;  // NOT_Gate not_2, 4 bits wide
  assign not_3_out = ~xor_3_out;  // NOT_Gate not_3, 4 bits wide
  assign xor_3_out = 4'b0011 ^ CRI[7:4];  // XOR_Gate xor_3, 4 bits wide
  and and_1 (and_1_out, not_1_out[0], not_1_out[1], not_1_out[2], not_1_out[3]);
  and and_2 (and_2_out, not_2_out[0], not_2_out[1], not_2_out[2], not_2_out[3]);
  and and_3 (and_3_out, not_3_out[0], not_3_out[1], not_3_out[2], not_3_out[3]);
  and and_4 (RetPEB, or_1_out, ActivationSignal);
  or or_1 (or_1_out, and_1_out, and_2_out, and_3_out);
  and and_5 (and_5_out, and_1_out, ActivationSignal);
  and and_6 (and_6_out, and_2_out, ActivationSignal);
  and and_7 (and_7_out, and_3_out, ActivationSignal);
  assign PEB = and_6_out ? CLE : 12'bz;  // Controlled_Buffer controlled_buffer_2
  assign PEB = and_5_out ? InternalExpression : 12'bz;  // Controlled_Buffer controlled_buffer_3
  assign PEB = and_7_out ? CRE : 12'bz;  // Controlled_Buffer controlled_buffer_4
  or or_2 (or_2_out, and_5_out, and_6_out, and_7_out);
  assign PIB_2 = or_2_out ? 8'h30 : 8'bz;  // Controlled_Buffer controlled_buffer_5

  assign CRI_2 = CLI_2;
  assign RetCLI = ActivationSignal;
  assign RetCRI = ActivationSignal;
  assign RetPIB = RetPEB;

  // Notes on the sheet:
  //   Marker Signal is 0011
  //   Marker Signal is 0011
endmodule

module BranchChop (
  input  Clock,
  input  [7:0] CLI,
  input  [7:0] CRI,
  input  [11:0] InternalExpression,
  output BraNew,
  output [11:0] NewValue
);

  wire and_1_out, and_2_out, or_1_out;
  wire [3:0] not_1_out, not_2_out, xor_1_out, xor_2_out;

  assign xor_1_out = CLI[7:4] ^ 4'b0001;  // XOR_Gate xor_1, 4 bits wide
  assign xor_2_out = CRI[7:4] ^ 4'b0001;  // XOR_Gate xor_2, 4 bits wide
  assign not_1_out = ~xor_1_out;  // NOT_Gate not_1, 4 bits wide
  assign not_2_out = ~xor_2_out;  // NOT_Gate not_2, 4 bits wide
  D_Flip_Flop d_ff_1 (.D(or_1_out), .clk(Clock), .Q(BraNew));  // open: Qn, preset, reset
  or or_1 (or_1_out, and_2_out, and_1_out);
  and and_1 (and_1_out, not_1_out[0], not_1_out[1], not_1_out[2], not_1_out[3]);
  and and_2 (and_2_out, not_2_out[0], not_2_out[1], not_2_out[2], not_2_out[3]);
  assign NewValue = and_2_out ? {4'b0000, InternalExpression[7:4], 3'b100, InternalExpression[0]} : 12'bz;  // Controlled_Buffer controlled_buffer_1
  assign NewValue = and_1_out ? {4'b0000, InternalExpression[11:8], 3'b100, InternalExpression[0]} : 12'bz;  // Controlled_Buffer controlled_buffer_2
endmodule

module CompareValue (
  input  ActivationSignal,
  input  Clock,
  input  Clear,
  input  [11:0] InternalValue,
  input  [11:0] PEB,
  input  [7:0] PIB,
  input  [7:0] CRI,
  input  [7:0] CLI,
  output ComCLI,
  output ComCLE,
  output ComCRI,
  output ComCRE,
  output ComPIB,
  output MarkForTransformation,
  output [7:0] CLI_2,
  output [7:0] CRI_2,
  output [11:0] CLE,
  output [11:0] CRE,
  output [7:0] PIB_2
);

  wire and_1_out, and_2_out, and_3_out, and_4_out, and_5_out, and_6_out, and_8_out, and_9_out, and_10_out,
       not_4_out, not_6_out, not_7_out, not_8_out, not_9_out, or_2_out;
  wire [2:0] not_1_out, xor_1_out;
  wire [3:0] not_2_out, not_5_out, xor_2_out, xor_4_out;
  wire [7:0] controlled_buffer_1_out, controlled_buffer_5_out, not_3_out, xor_3_out;

  assign xor_1_out = 3'b010 ^ InternalValue[10:8];  // XOR_Gate xor_1, 3 bits wide
  assign not_1_out = ~xor_1_out;  // NOT_Gate not_1, 3 bits wide
  assign not_2_out = ~xor_2_out;  // NOT_Gate not_2, 4 bits wide
  assign xor_2_out = 4'b0100 ^ CRI[7:4];  // XOR_Gate xor_2, 4 bits wide
  and and_1 (and_1_out, not_1_out[0], not_1_out[1], not_1_out[2]);
  assign xor_3_out = InternalValue[7:0] ^ PEB[7:0];  // XOR_Gate xor_3, 8 bits wide
  assign not_3_out = ~xor_3_out;  // NOT_Gate not_3, 8 bits wide
  and and_2 (and_2_out, not_2_out[0], not_2_out[1], not_2_out[2], not_2_out[3]);
  not not_4 (not_4_out, and_1_out);
  and and_3 (and_3_out, not_3_out[0], not_3_out[1], not_3_out[2], not_3_out[3], not_3_out[4], not_3_out[5], not_3_out[6], not_3_out[7]);
  assign controlled_buffer_1_out = and_2_out ? CRI : 8'bz;  // Controlled_Buffer controlled_buffer_1
  assign xor_4_out = 4'b0100 ^ CLI[7:4];  // XOR_Gate xor_4, 4 bits wide
  and and_4 (and_4_out, not_4_out, and_3_out);
  assign not_5_out = ~xor_4_out;  // NOT_Gate not_5, 4 bits wide
  assign controlled_buffer_1_out = and_5_out ? CLI : 8'bz;  // Controlled_Buffer controlled_buffer_2
  and and_5 (and_5_out, not_5_out[0], not_5_out[1], not_5_out[2], not_5_out[3]);
  not not_6 (not_6_out, and_2_out);
  and and_6 (and_6_out, not_6_out, not_7_out);
  not not_7 (not_7_out, and_5_out);
  or or_1 (ComPIB, ComCLE, and_8_out);
  and and_7 (ComCLE, and_1_out, ActivationSignal);
  not not_8 (not_8_out, and_1_out);
  assign CLI_2 = and_1_out ? PIB : 8'bz;  // Controlled_Buffer controlled_buffer_3
  assign CLE = and_1_out ? PEB : 12'bz;  // Controlled_Buffer controlled_buffer_4
  assign controlled_buffer_5_out = and_1_out ? controlled_buffer_1_out : 8'bz;  // Controlled_Buffer controlled_buffer_5
  assign controlled_buffer_1_out = and_6_out ? {8{1'b0}} : 8'bz;  // Controlled_Buffer controlled_buffer_6
  and and_8 (and_8_out, not_8_out, ActivationSignal);
  and and_9 (and_9_out, ActivationSignal, and_4_out);
  not not_9 (not_9_out, and_4_out);
  and and_10 (and_10_out, not_8_out, not_9_out);
  assign controlled_buffer_5_out = and_4_out ? 8'h40 : 8'bz;  // Controlled_Buffer controlled_buffer_7
  assign controlled_buffer_5_out = and_10_out ? {8{1'b0}} : 8'bz;  // Controlled_Buffer controlled_buffer_8
  or or_2 (or_2_out, MarkForTransformation, and_9_out);
  assign PIB_2 = ActivationSignal ? controlled_buffer_5_out : 8'bz;  // Controlled_Buffer controlled_buffer_9
  D_Flip_Flop d_ff_1 (.D(or_2_out), .clk(Clock), .Q(MarkForTransformation), .reset(Clear));  // open: Qn, preset

  assign ComCLI = ComCLE;
  assign ComCRE = ComCLE;
  assign ComCRI = ComCLE;
  assign CRE = CLE;
  assign CRI_2 = CLI_2;
endmodule

module ImmediateResolution (
  input  ActivationSignal,
  output ImmPIB,
  output [7:0] out_3
);

  assign out_3 = ActivationSignal ? 8'h10 : 8'bz;  // Controlled_Buffer controlled_buffer_1

  assign ImmPIB = ActivationSignal;
endmodule

module PrepareForTransformationAsAncestorInput (
  input  ActivationSignal,
  input  Clock,
  input  [3:0] SFS,
  input  [3:0] SBS,
  input  [3:0] RAM,
  input  [3:0] UniqueNodeID,
  input  [7:0] CLI,
  input  [7:0] CRI,
  input  [11:0] CLE,
  input  [11:0] CRE,
  input  [11:0] InternalExpression,
  output ptaPEB,
  output ptaCLI,
  output ptaSEL,
  output ptaStackClear,
  output ptaRAM,
  output ptaSFS,
  output ptaSBS,
  output ptaCRI,
  output ptaPIB,
  output [7:0] GeneralOuput,
  output [11:0] PEB,
  output [7:0] CLI_2,
  output [7:0] CRI_2,
  output [7:0] PIB
);

  wire and_1_out, and_2_out, and_3_out, and_4_out, and_5_out, and_6_out, and_7_out, and_8_out, and_9_out,
       and_10_out, and_11_out, and_12_out, and_13_out, and_14_out, and_15_out, and_16_out, and_17_out,
       and_18_out, and_19_out, and_20_out, and_21_out, and_22_out, and_23_out, and_24_out, and_26_out,
       and_28_out, d_ff_1_q, d_ff_2_q, d_ff_3_q, d_ff_4_q, d_ff_5_q, d_ff_6_q, d_ff_7_q, d_ff_8_q, d_ff_9_q,
       d_ff_10_q, not_1_out, not_9_out, not_10_out, or_1_out, or_4_out, or_5_out, or_7_out, or_8_out,
       or_9_out, or_11_out, or_12_out, or_13_out, or_14_out, or_15_out, or_16_out, or_17_out, or_18_out,
       or_19_out, or_20_out, or_21_out, or_22_out, or_23_out, or_24_out;
  wire [2:0] not_7_out, not_8_out, xor_6_out, xor_7_out;
  wire [3:0] adder_1_out, adder_2_out, not_2_out, not_3_out, not_4_out, not_5_out, not_6_out, xor_1_out,
       xor_2_out, xor_3_out, xor_4_out, xor_5_out;
  wire [11:0] controlled_buffer_2_out, register_1_q;

  not not_1 (not_1_out, or_1_out);
  assign xor_1_out = 4'b0000 ^ SFS;  // XOR_Gate xor_1, 4 bits wide
  assign xor_2_out = 4'b0011 ^ CLI[7:4];  // XOR_Gate xor_2, 4 bits wide
  assign xor_3_out = 4'b0011 ^ CRI[7:4];  // XOR_Gate xor_3, 4 bits wide
  D_Flip_Flop d_ff_1 (.D(and_1_out), .clk(Clock), .Q(d_ff_1_q));  // open: Qn, preset, reset
  and and_1 (and_1_out, ActivationSignal, not_1_out);
  assign not_2_out = ~xor_1_out;  // NOT_Gate not_2, 4 bits wide
  assign not_3_out = ~xor_4_out;  // NOT_Gate not_3, 4 bits wide
  assign xor_4_out = RAM ^ UniqueNodeID;  // XOR_Gate xor_4, 4 bits wide
  Adder #(.width(4)) adder_1 (.a(4'b0001), .b(SFS), .out(adder_1_out));  // open: cin, cout
  Adder #(.width(4)) adder_2 (.a(4'b0001), .b(SBS), .out(adder_2_out));  // open: cin, cout
  assign xor_5_out = SFS ^ SBS;  // XOR_Gate xor_5, 4 bits wide
  assign not_4_out = ~xor_5_out;  // NOT_Gate not_4, 4 bits wide
  assign not_5_out = ~xor_2_out;  // NOT_Gate not_5, 4 bits wide
  assign not_6_out = ~xor_3_out;  // NOT_Gate not_6, 4 bits wide
  and and_2 (and_2_out, and_3_out, and_4_out);
  or or_1 (or_1_out, and_3_out, or_4_out);
  and and_3 (and_3_out, ActivationSignal, d_ff_1_q);
  and and_4 (and_4_out, not_2_out[0], not_2_out[1], not_2_out[2], not_2_out[3]);
  and and_5 (and_5_out, and_3_out, and_4_out);
  and and_6 (and_6_out, not_3_out[0], not_3_out[1], not_3_out[2], not_3_out[3]);
  and and_7 (and_7_out, not_4_out[0], not_4_out[1], not_4_out[2], not_4_out[3]);
  and and_8 (and_8_out, not_5_out[0], not_5_out[1], not_5_out[2], not_5_out[3]);
  and and_9 (and_9_out, not_6_out[0], not_6_out[1], not_6_out[2], not_6_out[3]);
  or or_2 (ptaRAM, and_2_out, or_13_out);
  D_Flip_Flop d_ff_2 (.D(and_3_out), .clk(Clock), .Q(d_ff_2_q));  // open: Qn, preset, reset
  assign GeneralOuput = and_5_out ? {4'b0000, UniqueNodeID} : 8'bz;  // Controlled_Buffer controlled_buffer_1
  assign controlled_buffer_2_out = and_8_out ? CLE : 12'bz;  // Controlled_Buffer controlled_buffer_2
  assign controlled_buffer_2_out = and_9_out ? CRE : 12'bz;  // Controlled_Buffer controlled_buffer_3
  assign controlled_buffer_2_out = and_6_out ? InternalExpression : 12'bz;  // Controlled_Buffer controlled_buffer_4
  or or_3 (ptaSFS, and_10_out, or_8_out);
  and and_10 (and_10_out, and_11_out, and_4_out);
  or or_4 (or_4_out, and_11_out, or_5_out);
  and and_11 (and_11_out, ActivationSignal, d_ff_2_q);
  and and_12 (and_12_out, and_11_out, and_4_out);
  assign GeneralOuput = and_12_out ? {4'b0000, adder_1_out} : 8'bz;  // Controlled_Buffer controlled_buffer_5
  or or_5 (or_5_out, and_13_out, or_9_out);
  D_Flip_Flop d_ff_3 (.D(and_11_out), .clk(Clock), .Q(d_ff_3_q));  // open: Qn, preset, reset
  or or_6 (ptaCLI, and_13_out, or_7_out);
  and and_13 (and_13_out, ActivationSignal, d_ff_3_q);
  Register #(.width(12)) register_1 (
    .D(controlled_buffer_2_out), .en(and_13_out), .clk(Clock), .Q(register_1_q));  // open: clr
  assign PEB = and_13_out ? controlled_buffer_2_out : 12'bz;  // Controlled_Buffer controlled_buffer_6
  assign CLI_2 = and_13_out ? {4'b0101, RAM} : 8'bz;  // Controlled_Buffer controlled_buffer_7
  assign CRI_2 = and_13_out ? {4'b0101, RAM} : 8'bz;  // Controlled_Buffer controlled_buffer_8
  or or_7 (or_7_out, or_12_out, and_15_out);
  or or_8 (or_8_out, and_21_out, and_14_out);
  or or_9 (or_9_out, and_15_out, or_14_out);
  D_Flip_Flop d_ff_4 (.D(and_13_out), .clk(Clock), .Q(d_ff_4_q));  // open: Qn, preset, reset
  assign not_7_out = ~xor_6_out;  // NOT_Gate not_7, 3 bits wide
  assign xor_6_out = 3'b101 ^ register_1_q[10:8];  // XOR_Gate xor_6, 3 bits wide
  assign not_8_out = ~xor_7_out;  // NOT_Gate not_8, 3 bits wide
  assign xor_7_out = 3'b001 ^ register_1_q[10:8];  // XOR_Gate xor_7, 3 bits wide
  or or_10 (ptaSEL, and_15_out, or_11_out);
  and and_14 (and_14_out, and_15_out, and_19_out);
  and and_15 (and_15_out, ActivationSignal, d_ff_4_q);
  assign GeneralOuput = and_15_out ? {4'b0000, adder_1_out} : 8'bz;  // Controlled_Buffer controlled_buffer_9
  assign PEB = and_15_out ? register_1_q : 12'bz;  // Controlled_Buffer controlled_buffer_10
  not not_9 (not_9_out, and_16_out);
  and and_16 (and_16_out, not_7_out[0], not_7_out[1], not_7_out[2]);
  and and_17 (and_17_out, not_8_out[0], not_8_out[1], not_8_out[2]);
  or or_11 (or_11_out, or_18_out, and_20_out);
  or or_12 (or_12_out, or_19_out, and_20_out);
  or or_13 (or_13_out, and_23_out, and_18_out);
  and and_18 (and_18_out, and_19_out, and_20_out);
  D_Flip_Flop d_ff_5 (.D(and_15_out), .clk(Clock), .Q(d_ff_5_q));  // open: Qn, preset, reset
  and and_19 (and_19_out, not_9_out, not_10_out);
  or or_14 (or_14_out, and_20_out, or_16_out);
  and and_20 (and_20_out, ActivationSignal, d_ff_5_q);
  or or_15 (or_15_out, and_20_out, or_17_out);
  assign PEB = or_15_out ? register_1_q : 12'bz;  // Controlled_Buffer controlled_buffer_11
  or or_16 (or_16_out, and_22_out, or_21_out);
  D_Flip_Flop d_ff_6 (.D(and_20_out), .clk(Clock), .Q(d_ff_6_q));  // open: Qn, preset, reset
  or or_17 (or_17_out, and_22_out, or_22_out);
  assign GeneralOuput = and_18_out ? {4'b0000, register_1_q[7:4]} : 8'bz;  // Controlled_Buffer controlled_buffer_12
  or or_18 (or_18_out, and_23_out, and_21_out);
  or or_19 (or_19_out, or_20_out, and_21_out);
  and and_21 (and_21_out, not_10_out, and_22_out);
  and and_22 (and_22_out, ActivationSignal, d_ff_6_q);
  not not_10 (not_10_out, and_17_out);
  D_Flip_Flop d_ff_7 (.D(and_22_out), .clk(Clock), .Q(d_ff_7_q));  // open: Qn, preset, reset
  assign GeneralOuput = and_21_out ? {4'b0000, adder_1_out} : 8'bz;  // Controlled_Buffer controlled_buffer_13
  or or_20 (or_20_out, or_23_out, and_23_out);
  and and_23 (and_23_out, not_10_out, and_24_out);
  buf or_21 (or_21_out, and_24_out);  // OR_Gate
  and and_24 (and_24_out, ActivationSignal, d_ff_7_q);
  or or_22 (or_22_out, and_24_out, or_24_out);
  assign GeneralOuput = and_24_out ? {4'b0000, register_1_q[3:0]} : 8'bz;  // Controlled_Buffer controlled_buffer_14
  or or_23 (or_23_out, ptaPIB, ptaSBS);
  D_Flip_Flop d_ff_8 (.D(and_24_out), .clk(Clock), .Q(d_ff_8_q));  // open: Qn, preset, reset
  or or_24 (or_24_out, ptaSBS, and_28_out);
  D_Flip_Flop d_ff_9 (.D(ptaSBS), .clk(Clock), .Q(d_ff_9_q));  // open: Qn, preset, reset
  and and_25 (ptaSBS, ActivationSignal, d_ff_8_q);
  assign GeneralOuput = ptaSBS ? {4'b0000, adder_2_out} : 8'bz;  // Controlled_Buffer controlled_buffer_15
  D_Flip_Flop d_ff_10 (.D(and_26_out), .clk(Clock), .Q(d_ff_10_q));  // open: Qn, preset, reset
  and and_26 (and_26_out, ActivationSignal, d_ff_9_q);
  and and_27 (ptaPIB, and_28_out, and_7_out);
  and and_28 (and_28_out, ActivationSignal, d_ff_10_q);
  assign PIB = ptaPIB ? 8'h10 : 8'bz;  // Controlled_Buffer controlled_buffer_16

  assign ptaCRI = ptaCLI;
  assign ptaPEB = ptaCLI;
  assign ptaStackClear = ptaPIB;

  // Notes on the sheet:
  //   New SFS
  //   New SBS
  //   RAM on == Write
  //   off == Read
  //   SEL off == SBS
  //   on == SFS
endmodule

module PrepareForTransformationAsDecendantInput (
  input  ActivationSignal,
  input  Clock,
  input  TransformMark,
  input  [11:0] InExp,
  input  [3:0] SFS,
  input  [3:0] SBS,
  input  [3:0] UniqueNodeID,
  input  [3:0] RAM,
  input  [3:0] NewNodeID,
  input  [7:0] PIB,
  input  [2:0] Buffer,
  input  [11:0] PEB,
  input  [7:0] CLI,
  input  [7:0] CRI,
  output ptdPIB,
  output ptdSEL,
  output ptdNEW,
  output PtdBUF,
  output ptdCRI,
  output PtdEXP,
  output ptdStackclear,
  output ptdCLC,
  output ptdRAM,
  output ptdSFS,
  output PtdToggleChildren,
  output ptdSBS,
  output ptdCLI,
  output ptdCompareValueClear,
  output ptdCRE,
  output ptdCLE,
  output [7:0] Output,
  output [7:0] CLI_2,
  output [11:0] CLE,
  output [7:0] CRI_2,
  output [11:0] CRE,
  output [7:0] PIB_2,
  output [11:0] NewExpression
);

  wire and_1_out, and_2_out, and_3_out, and_4_out, and_6_out, and_7_out, and_8_out, and_9_out, and_10_out,
       and_11_out, and_12_out, and_13_out, and_14_out, and_15_out, and_16_out, and_17_out, and_18_out,
       and_19_out, and_20_out, and_21_out, and_22_out, and_23_out, and_24_out, and_26_out, and_27_out,
       and_28_out, and_29_out, and_30_out, and_31_out, and_32_out, and_33_out, and_34_out, and_35_out,
       and_36_out, and_37_out, and_38_out, and_39_out, and_40_out, and_41_out, and_42_out, and_43_out,
       and_44_out, and_45_out, and_46_out, and_47_out, and_48_out, and_49_out, and_50_out,
       controlled_buffer_1_out, d_ff_1_q, d_ff_2_q, d_ff_3_q, d_ff_4_q, d_ff_5_q, d_ff_6_q, d_ff_7_q,
       d_ff_8_q, d_ff_9_q, d_ff_10_q, not_2_out, not_3_out, not_12_out, not_13_out, not_14_out, not_17_out,
       not_18_out, not_19_out, not_20_out, not_21_out, not_22_out, not_23_out, not_24_out, not_25_out,
       not_26_out, or_1_out, or_3_out, or_5_out, or_6_out, or_7_out, or_10_out, or_12_out, or_13_out,
       or_14_out, or_16_out, or_17_out, or_18_out, or_19_out, or_20_out, or_21_out, or_22_out, or_23_out,
       or_24_out, or_25_out;
  wire [2:0] not_1_out, not_6_out, not_7_out, not_10_out, not_11_out, xor_1_out, xor_3_out, xor_4_out,
       xor_8_out, xor_9_out;
  wire [3:0] adder_1_out, adder_2_out, controlled_buffer_14_out, controlled_buffer_23_out, not_4_out,
       not_5_out, not_16_out, register_1_q, xor_2_out, xor_7_out, xor_10_out;
  wire [7:0] controlled_buffer_4_out, not_8_out, not_9_out, xor_5_out, xor_6_out;
  wire [11:0] controlled_buffer_6_out;

  assign xor_1_out = 3'b010 ^ InExp[10:8];  // XOR_Gate xor_1, 3 bits wide
  assign not_1_out = ~xor_1_out;  // NOT_Gate not_1, 3 bits wide
  and and_1 (and_1_out, ActivationSignal, TransformMark);
  and and_2 (and_2_out, not_1_out[0], not_1_out[2]);
  and and_3 (and_3_out, and_2_out, ActivationSignal);
  not not_2 (not_2_out, and_3_out);
  not not_3 (not_3_out, or_1_out);
  assign controlled_buffer_1_out = not_2_out ? and_1_out : 1'bz;  // Controlled_Buffer controlled_buffer_1
  assign xor_2_out = 4'b0000 ^ SFS;  // XOR_Gate xor_2, 4 bits wide
  assign xor_3_out = 3'b001 ^ Buffer;  // XOR_Gate xor_3, 3 bits wide
  assign xor_4_out = 3'b001 ^ PEB[10:8];  // XOR_Gate xor_4, 3 bits wide
  assign xor_5_out = 8'h20 ^ CLI;  // XOR_Gate xor_5, 8 bits wide
  assign xor_6_out = 8'h20 ^ CRI;  // XOR_Gate xor_6, 8 bits wide
  D_Flip_Flop d_ff_1 (.D(and_4_out), .clk(Clock), .Q(d_ff_1_q));  // open: Qn, preset, reset
  and and_4 (and_4_out, controlled_buffer_1_out, not_3_out);
  assign not_4_out = ~xor_2_out;  // NOT_Gate not_4, 4 bits wide
  Adder #(.width(4)) adder_1 (.a(4'b0001), .b(SFS), .out(adder_1_out));  // open: cin, cout
  Adder #(.width(4)) adder_2 (.a(4'b0001), .b(SBS), .out(adder_2_out));  // open: cin, cout
  assign not_5_out = ~xor_7_out;  // NOT_Gate not_5, 4 bits wide
  assign xor_7_out = SFS ^ SBS;  // XOR_Gate xor_7, 4 bits wide
  assign not_6_out = ~xor_3_out;  // NOT_Gate not_6, 3 bits wide
  assign not_7_out = ~xor_4_out;  // NOT_Gate not_7, 3 bits wide
  assign not_8_out = ~xor_5_out;  // NOT_Gate not_8, 8 bits wide
  assign not_9_out = ~xor_6_out;  // NOT_Gate not_9, 8 bits wide
  and and_5 (ptdCLC, and_6_out, and_7_out);
  or or_1 (or_1_out, and_6_out, or_5_out);
  and and_6 (and_6_out, controlled_buffer_1_out, d_ff_1_q);
  and and_7 (and_7_out, not_4_out[0], not_4_out[1], not_4_out[2], not_4_out[3]);
  and and_8 (and_8_out, and_6_out, and_7_out);
  and and_9 (and_9_out, not_5_out[0], not_5_out[1], not_5_out[2], not_5_out[3]);
  and and_10 (and_10_out, not_6_out[0], not_6_out[1], not_6_out[2]);
  and and_11 (and_11_out, not_7_out[0], not_7_out[1], not_7_out[2]);
  and and_12 (and_12_out, not_8_out[0], not_8_out[1], not_8_out[2], not_8_out[3], not_8_out[4], not_8_out[5], not_8_out[6], not_8_out[7]);
  and and_13 (and_13_out, not_9_out[0], not_9_out[1], not_9_out[2], not_9_out[3], not_9_out[4], not_9_out[5], not_9_out[6], not_9_out[7]);
  or or_2 (ptdRAM, ptdCLC, or_13_out);
  D_Flip_Flop d_ff_2 (.D(and_6_out), .clk(Clock), .Q(d_ff_2_q));  // open: Qn, preset, reset
  assign Output = and_8_out ? {4'b0000, UniqueNodeID} : 8'bz;  // Controlled_Buffer controlled_buffer_2
  assign xor_8_out = 3'b000 ^ Buffer;  // XOR_Gate xor_8, 3 bits wide
  assign not_10_out = ~xor_8_out;  // NOT_Gate not_10, 3 bits wide
  assign not_11_out = ~xor_9_out;  // NOT_Gate not_11, 3 bits wide
  assign xor_9_out = 3'b101 ^ PEB[10:8];  // XOR_Gate xor_9, 3 bits wide
  or or_3 (or_3_out, and_12_out, and_13_out);
  or or_4 (ptdSFS, and_14_out, or_19_out);
  and and_14 (and_14_out, and_15_out, and_7_out);
  or or_5 (or_5_out, and_15_out, or_6_out);
  and and_15 (and_15_out, controlled_buffer_1_out, d_ff_2_q);
  and and_16 (and_16_out, and_15_out, and_7_out);
  assign Output = and_16_out ? {4'b0000, adder_1_out} : 8'bz;  // Controlled_Buffer controlled_buffer_3
  and and_17 (and_17_out, not_10_out[0], not_10_out[1], not_10_out[2]);
  not not_12 (not_12_out, and_11_out);
  not not_13 (not_13_out, and_18_out);
  and and_18 (and_18_out, not_11_out[0], not_11_out[1], not_11_out[2]);
  assign controlled_buffer_4_out = not_14_out ? {8{1'b0}} : 8'bz;  // Controlled_Buffer controlled_buffer_4
  not not_14 (not_14_out, or_3_out);
  or or_6 (or_6_out, and_20_out, or_10_out);
  D_Flip_Flop d_ff_3 (.D(and_15_out), .clk(Clock), .Q(d_ff_3_q));  // open: Qn, preset, reset
  and and_19 (and_19_out, not_12_out, not_13_out);
  assign controlled_buffer_4_out = or_3_out ? 8'h20 : 8'bz;  // Controlled_Buffer controlled_buffer_5
  and and_20 (and_20_out, controlled_buffer_1_out, d_ff_3_q);
  Register #(.width(4)) register_1 (.D(RAM), .en(and_20_out), .clk(Clock), .Q(register_1_q));  // open: clr
  not not_15 (PtdToggleChildren, or_7_out);
  or or_7 (or_7_out, and_10_out, and_17_out);
  or or_8 (ptdSEL, and_22_out, or_17_out);
  D_Flip_Flop d_ff_4 (.D(and_20_out), .clk(Clock), .Q(d_ff_4_q));  // open: Qn, preset, reset
  assign not_16_out = ~xor_10_out;  // NOT_Gate not_16, 4 bits wide
  assign xor_10_out = register_1_q ^ UniqueNodeID;  // XOR_Gate xor_10, 4 bits wide
  assign controlled_buffer_6_out = not_17_out ? {1'b0, PEB[10:8], {8{1'b0}}} : 12'bz;  // Controlled_Buffer controlled_buffer_6
  not not_17 (not_17_out, and_11_out);
  or or_9 (ptdNEW, and_21_out, and_35_out);
  and and_21 (and_21_out, and_22_out, and_19_out);
  or or_10 (or_10_out, and_22_out, or_14_out);
  and and_22 (and_22_out, controlled_buffer_1_out, d_ff_4_q);
  and and_23 (and_23_out, not_16_out[0], not_16_out[1], not_16_out[2], not_16_out[3]);
  assign controlled_buffer_6_out = and_11_out ? {1'b0, PEB[10:0]} : 12'bz;  // Controlled_Buffer controlled_buffer_7
  or or_11 (ptdCLE, or_12_out, or_16_out);
  or or_12 (or_12_out, and_3_out, and_24_out);
  and and_24 (and_24_out, not_18_out, and_22_out);
  and and_25 (PtdBUF, and_23_out, and_22_out);
  not not_18 (not_18_out, and_23_out);
  not not_19 (not_19_out, and_23_out);
  and and_26 (and_26_out, and_23_out, and_22_out);
  and and_27 (and_27_out, not_19_out, and_22_out);
  assign Output = and_26_out ? {{5{1'b0}}, PEB[10:8]} : 8'bz;  // Controlled_Buffer controlled_buffer_8
  D_Flip_Flop d_ff_5 (.D(and_22_out), .clk(Clock), .Q(d_ff_5_q));  // open: Qn, preset, reset
  assign CLI_2 = and_27_out ? {4'b0010, register_1_q} : 8'bz;  // Controlled_Buffer controlled_buffer_9
  assign CLE = and_27_out ? controlled_buffer_6_out : 12'bz;  // Controlled_Buffer controlled_buffer_10
  assign CRI_2 = and_27_out ? {4'b0010, register_1_q} : 8'bz;  // Controlled_Buffer controlled_buffer_11
  assign CRE = and_27_out ? controlled_buffer_6_out : 12'bz;  // Controlled_Buffer controlled_buffer_12
  assign NewExpression = and_27_out ? {1'b0, PEB[10:8], {8{1'b0}}} : 12'bz;  // Controlled_Buffer controlled_buffer_13
  not not_20 (not_20_out, and_11_out);
  or or_13 (or_13_out, and_41_out, and_31_out);
  or or_14 (or_14_out, and_28_out, or_20_out);
  and and_28 (and_28_out, controlled_buffer_1_out, d_ff_5_q);
  assign controlled_buffer_14_out = not_21_out ? NewNodeID : 4'bz;  // Controlled_Buffer controlled_buffer_14
  not not_21 (not_21_out, or_7_out);
  assign controlled_buffer_14_out = or_7_out ? PEB[7:4] : 4'bz;  // Controlled_Buffer controlled_buffer_15
  or or_15 (PtdEXP, and_29_out, or_21_out);
  or or_16 (or_16_out, and_44_out, and_30_out);
  or or_17 (or_17_out, or_18_out, and_28_out);
  and and_29 (and_29_out, and_23_out, and_28_out);
  and and_30 (and_30_out, not_22_out, and_32_out);
  and and_31 (and_31_out, and_19_out, and_28_out);
  not not_22 (not_22_out, and_23_out);
  and and_32 (and_32_out, and_19_out, and_28_out);
  not not_23 (not_23_out, and_23_out);
  and and_33 (and_33_out, and_23_out, and_28_out);
  and and_34 (and_34_out, not_23_out, and_32_out);
  assign NewExpression = and_33_out ? {InExp[11:8], controlled_buffer_14_out, InExp[3:0]} : 12'bz;  // Controlled_Buffer controlled_buffer_16
  assign CLI_2 = and_34_out ? {4'b0011, register_1_q} : 8'bz;  // Controlled_Buffer controlled_buffer_17
  assign CLE = and_34_out ? {4'b0000, PEB[7:4], 4'b0000} : 12'bz;  // Controlled_Buffer controlled_buffer_18
  assign CRI_2 = and_34_out ? {4'b0011, register_1_q} : 8'bz;  // Controlled_Buffer controlled_buffer_19
  assign CRE = and_34_out ? {4'b0000, PEB[7:4], 4'b0000} : 12'bz;  // Controlled_Buffer controlled_buffer_20
  or or_18 (or_18_out, or_23_out, and_36_out);
  or or_19 (or_19_out, and_46_out, and_37_out);
  D_Flip_Flop d_ff_6 (.D(and_28_out), .clk(Clock), .Q(d_ff_6_q));  // open: Qn, preset, reset
  assign Output = and_28_out ? {4'b0000, NewNodeID} : 8'bz;  // Controlled_Buffer controlled_buffer_21
  and and_35 (and_35_out, and_36_out, not_20_out);
  or or_20 (or_20_out, and_36_out, or_22_out);
  and and_36 (and_36_out, controlled_buffer_1_out, d_ff_6_q);
  and and_37 (and_37_out, and_19_out, and_36_out);
  D_Flip_Flop d_ff_7 (.D(and_36_out), .clk(Clock), .Q(d_ff_7_q));  // open: Qn, preset, reset
  and and_38 (and_38_out, and_19_out, and_36_out);
  assign Output = and_38_out ? {4'b0000, adder_1_out} : 8'bz;  // Controlled_Buffer controlled_buffer_22
  or or_21 (or_21_out, ptdCompareValueClear, and_40_out);
  or or_22 (or_22_out, and_39_out, or_24_out);
  and and_39 (and_39_out, controlled_buffer_1_out, d_ff_7_q);
  assign controlled_buffer_23_out = not_24_out ? NewNodeID : 4'bz;  // Controlled_Buffer controlled_buffer_23
  not not_24 (not_24_out, or_7_out);
  assign controlled_buffer_23_out = or_7_out ? PEB[3:0] : 4'bz;  // Controlled_Buffer controlled_buffer_24
  and and_40 (and_40_out, and_23_out, and_39_out);
  and and_41 (and_41_out, not_20_out, and_39_out);
  not not_25 (not_25_out, and_23_out);
  and and_42 (and_42_out, not_20_out, and_39_out);
  not not_26 (not_26_out, and_23_out);
  and and_43 (and_43_out, and_23_out, and_39_out);
  assign NewExpression = and_43_out ? {InExp[11:4], controlled_buffer_23_out} : 12'bz;  // Controlled_Buffer controlled_buffer_25
  or or_23 (or_23_out, and_47_out, and_39_out);
  and and_44 (and_44_out, not_25_out, and_42_out);
  and and_45 (and_45_out, not_26_out, and_42_out);
  assign CLI_2 = and_45_out ? {4'b0100, register_1_q} : 8'bz;  // Controlled_Buffer controlled_buffer_26
  assign CLE = and_45_out ? {4'b0000, PEB[3:0], 4'b0000} : 12'bz;  // Controlled_Buffer controlled_buffer_27
  assign CRI_2 = and_45_out ? {4'b0100, register_1_q} : 8'bz;  // Controlled_Buffer controlled_buffer_28
  assign CRE = and_45_out ? {4'b0000, PEB[3:0], 4'b0000} : 12'bz;  // Controlled_Buffer controlled_buffer_29
  D_Flip_Flop d_ff_8 (.D(and_39_out), .clk(Clock), .Q(d_ff_8_q));  // open: Qn, preset, reset
  assign Output = and_39_out ? {4'b0000, NewNodeID} : 8'bz;  // Controlled_Buffer controlled_buffer_30
  or or_24 (or_24_out, and_47_out, or_25_out);
  and and_46 (and_46_out, not_20_out, and_47_out);
  D_Flip_Flop d_ff_9 (.D(and_47_out), .clk(Clock), .Q(d_ff_9_q));  // open: Qn, preset, reset
  and and_47 (and_47_out, controlled_buffer_1_out, d_ff_8_q);
  and and_48 (and_48_out, not_20_out, and_47_out);
  assign Output = and_48_out ? {4'b0000, adder_1_out} : 8'bz;  // Controlled_Buffer controlled_buffer_31
  or or_25 (or_25_out, and_49_out, and_50_out);
  or or_26 (ptdSBS, and_3_out, and_49_out);
  D_Flip_Flop d_ff_10 (.D(and_49_out), .clk(Clock), .Q(d_ff_10_q));  // open: Qn, preset, reset
  and and_49 (and_49_out, controlled_buffer_1_out, d_ff_9_q);
  assign Output = and_49_out ? {4'b0000, adder_2_out} : 8'bz;  // Controlled_Buffer controlled_buffer_32
  and and_50 (and_50_out, controlled_buffer_1_out, d_ff_10_q);
  and and_51 (ptdCompareValueClear, and_50_out, and_9_out);
  assign PIB_2 = ptdCompareValueClear ? 8'h2 : 8'bz;  // Controlled_Buffer controlled_buffer_33
  assign PIB_2 = and_3_out ? controlled_buffer_4_out : 8'bz;  // Controlled_Buffer controlled_buffer_34
  assign NewExpression = ptdCompareValueClear ? {InExp[11], Buffer, PEB[7:0]} : 12'bz;  // Controlled_Buffer controlled_buffer_35
  assign CLI_2 = and_3_out ? PIB : 8'bz;  // Controlled_Buffer controlled_buffer_36
  assign CRI_2 = and_3_out ? PIB : 8'bz;  // Controlled_Buffer controlled_buffer_37
  assign CLE = and_3_out ? PEB : 12'bz;  // Controlled_Buffer controlled_buffer_38
  assign CRE = and_3_out ? PEB : 12'bz;  // Controlled_Buffer controlled_buffer_39

  assign ptdCLI = ptdCLE;
  assign ptdCRE = ptdCLE;
  assign ptdCRI = ptdCLE;
  assign ptdPIB = ptdCompareValueClear;
  assign ptdStackclear = ptdCompareValueClear;

  // Notes on the sheet:
  //   Clear Children
  //   New SFS
  //   New SBS
  //   RAM on == Write
  //   off == Read
endmodule

module FunctionCoreLogic (
  input  ActivationSignal,
  input  UnreduceableFlag,
  input  Clock,
  input  [11:0] PEB,
  input  [11:0] InternalExpression,
  input  [11:0] CLE,
  input  [7:0] CRI,
  output CoreCRI,
  output CorePIB,
  output CoreNew,
  output CoreCRE,
  output [11:0] CRE,
  output [7:0] CRI_2,
  output [7:0] PIB,
  output [11:0] New
);

  wire and_1_out, and_2_out, and_3_out, and_4_out, and_5_out, and_6_out, and_7_out, and_8_out, and_9_out,
       and_10_out, and_11_out, and_12_out, and_13_out, d_ff_1_q, d_ff_2_q, d_ff_3_q, d_ff_4_q, d_ff_5_q,
       not_1_out, not_3_out, not_5_out, not_6_out, or_1_out, or_3_out, or_4_out, or_5_out, or_6_out, or_8_out;
  wire [3:0] not_2_out, not_4_out, xor_1_out, xor_2_out;

  not not_1 (not_1_out, UnreduceableFlag);
  and and_1 (and_1_out, PEB[11], InternalExpression[11]);
  assign not_2_out = ~xor_1_out;  // NOT_Gate not_2, 4 bits wide
  assign xor_1_out = 4'b0100 ^ CRI[7:4];  // XOR_Gate xor_1, 4 bits wide
  not not_3 (not_3_out, or_1_out);
  D_Flip_Flop d_ff_1 (.D(and_2_out), .clk(Clock), .Q(d_ff_1_q));  // open: Qn, preset, reset
  and and_2 (and_2_out, not_3_out, and_3_out);
  and and_3 (and_3_out, ActivationSignal, not_1_out, and_1_out);
  and and_4 (and_4_out, not_2_out[0], not_2_out[1], not_2_out[2], not_2_out[3]);
  or or_1 (or_1_out, or_4_out, and_5_out);
  and and_5 (and_5_out, ActivationSignal, d_ff_1_q);
  assign xor_2_out = 4'b0001 ^ CRI[7:4];  // XOR_Gate xor_2, 4 bits wide
  assign not_4_out = ~xor_2_out;  // NOT_Gate not_4, 4 bits wide
  or or_2 (CoreCRE, and_5_out, and_7_out, and_11_out);
  D_Flip_Flop d_ff_2 (.D(and_5_out), .clk(Clock), .Q(d_ff_2_q));  // open: Qn, preset, reset
  or or_3 (or_3_out, and_5_out, and_7_out);
  and and_6 (and_6_out, not_4_out[0], not_4_out[1], not_4_out[2], not_4_out[3]);
  or or_4 (or_4_out, or_5_out, and_7_out);
  and and_7 (and_7_out, ActivationSignal, d_ff_2_q);
  assign CRE = or_3_out ? CLE : 12'bz;  // Controlled_Buffer controlled_buffer_1
  assign CRI_2 = or_3_out ? 8'h60 : 8'bz;  // Controlled_Buffer controlled_buffer_2
  or or_5 (or_5_out, CoreNew, and_12_out, and_11_out);
  and and_8 (and_8_out, and_7_out, and_4_out);
  not not_5 (not_5_out, and_6_out);
  and and_9 (and_9_out, and_7_out, not_6_out);
  not not_6 (not_6_out, and_4_out);
  and and_10 (and_10_out, and_11_out, not_5_out);
  or or_6 (or_6_out, and_10_out, and_8_out);
  D_Flip_Flop d_ff_3 (.D(or_6_out), .clk(Clock), .Q(d_ff_3_q));  // open: Qn, preset, reset
  D_Flip_Flop d_ff_4 (.D(and_9_out), .clk(Clock), .Q(d_ff_4_q));  // open: Qn, preset, reset
  and and_11 (and_11_out, ActivationSignal, d_ff_3_q);
  and and_12 (and_12_out, ActivationSignal, d_ff_4_q);
  or or_7 (CorePIB, and_11_out, and_12_out);
  and and_13 (and_13_out, and_11_out, and_6_out);
  assign CRE = and_11_out ? PEB : 12'bz;  // Controlled_Buffer controlled_buffer_3
  assign CRI_2 = and_11_out ? 8'h90 : 8'bz;  // Controlled_Buffer controlled_buffer_4
  assign PIB = and_11_out ? 8'h80 : 8'bz;  // Controlled_Buffer controlled_buffer_5
  D_Flip_Flop d_ff_5 (.D(or_8_out), .clk(Clock), .Q(d_ff_5_q));  // open: Qn, preset, reset
  or or_8 (or_8_out, and_13_out, and_12_out);
  assign PIB = and_12_out ? 8'h70 : 8'bz;  // Controlled_Buffer controlled_buffer_6
  and and_14 (CoreNew, ActivationSignal, d_ff_5_q);
  assign New = CoreNew ? {PEB[11], 7'b1000000, PEB[3:0]} : 12'bz;  // Controlled_Buffer controlled_buffer_7

  assign CoreCRI = CoreCRE;
endmodule
